// Logisim project HERA_2.circ as structural Verilog: 38 circuits, main circuit main
module main (
);

  wire CLK, comparator_1_eq, comparator_2_gt, comparator_3_eq, comparator_4_eq, comparator_5_gt,
       comparator_6_eq, currently_interrupted, GET_CHAR, GET_CHAR_keyboard0, GET_CHAR_keyboard1, keyboard,
       not_1_out, PUT_CHAR, PUT_CHAR_screen0, PUT_CHAR_screen1, screen;
  wire [3:0] _0_3, _4_7, _8_11, Op;
  wire [6:0] char_out, keyboard_1_out;

  Clock clock_1 (.out(CLK));
  Keyboard keyboard_1 (.clk(CLK), .re(not_1_out), .data(keyboard_1_out));  // open: clr, avail
  not not_1 (not_1_out, currently_interrupted);
  Comparator #(.width(4)) comparator_1 (.a(Op), .b(4'b0001), .eq(comparator_1_eq));  // open: gt, lt
  Comparator #(.width(4)) comparator_2 (.a(_8_11), .b(4'b0000), .gt(comparator_2_gt));  // open: eq, lt
  Comparator #(.width(4)) comparator_3 (.a(_0_3), .b(4'b0000), .eq(comparator_3_eq));  // open: gt, lt
  Comparator #(.width(4)) comparator_4 (.a(Op), .b(4'b0001), .eq(comparator_4_eq));  // open: gt, lt
  Comparator #(.width(4)) comparator_5 (.a(_8_11), .b(4'b0000), .gt(comparator_5_gt));  // open: eq, lt
  Comparator #(.width(4)) comparator_6 (.a(_0_3), .b(4'b0001), .eq(comparator_6_eq));  // open: gt, lt
  and and_1 (PUT_CHAR, comparator_1_eq, comparator_2_gt, comparator_3_eq);
  and and_2 (GET_CHAR, comparator_4_eq, comparator_5_gt, comparator_6_eq);
  processor processor_1 (
    .CLK(CLK), .keyboard1_out(keyboard_1_out), .char_out(char_out), .screen_number(screen),
    .keyboard_to_read_from(keyboard), .Op_code({Op, _8_11, _4_7, _0_3}),
    .currently_interrupted(currently_interrupted));
  TTY tty_1 (.data(char_out), .clk(CLK), .we(PUT_CHAR_screen1));  // open: clr
  and and_3 (PUT_CHAR_screen0, PUT_CHAR, ~screen);  // AND_Gate
  and and_4 (PUT_CHAR_screen1, PUT_CHAR, screen);
  and and_5 (GET_CHAR_keyboard0, GET_CHAR, ~keyboard);  // AND_Gate
  and and_6 (GET_CHAR_keyboard1, GET_CHAR, keyboard);

  // Other names for the same wires on the sheet: Op_code[15:0] = {Op, _8_11, _4_7, _0_3}
endmodule

module processor (
  input  CLK,
  input  [6:0] keyboard1_out,
  output [6:0] char_out,
  output screen_number,
  output keyboard_to_read_from,
  output [15:0] Op_code,
  output currently_interrupted
);

  wire ALSU_carry_out, ALSU_overflow, and_1_out, and_3_out, BRANCH_branch, CALL_RETURN,
       called_interrupt_handler_yet, comparator_1_eq, comparator_2_eq, comparator_3_eq, F0, F1, F2, F3, F4,
       load, load_store, not_1_out, not_2_out, not_3_out, or_1_out, resolved_interrupt_handler_yet;
  wire [1:0] counter_1_q;
  wire [2:0] thread_number;
  wire [6:0] cur_char;
  wire [15:0] ALSU_out, BRANCH_pc_out, CALL_INTERRUPT_OP_code, PC_in, R0, R1, R2, R3, R4, R5, R6, R7, R8, R9,
       R10, R11, R12, R13, R14, R15, R_a, R_b, R_d, ram_1_ram_address, RAM_out, ROM_Op_code;

  and and_1 (and_1_out, ~called_interrupt_handler_yet, currently_interrupted);  // AND_Gate
  BRANCH BRANCH (
    .Op_code(Op_code), .PC_in(PC_in), .R_b(R_b), .R13(R13), .CALL_RETURN(CALL_RETURN), .F0(F0), .F1(F1),
    .F2(F2), .F3(F3), .called_interrupt_handler_yet(called_interrupt_handler_yet),
    .interrupted_this_cycle(currently_interrupted), .PC_out(BRANCH_pc_out), .branch(BRANCH_branch));
  Counter #(.width(2), .max('h3)) counter_1 (
    .Q(counter_1_q), .clk(CLK), .clr(not_1_out));  // open: load, D, count, carry
  not not_1 (not_1_out, currently_interrupted);
  not not_2 (not_2_out, BRANCH_branch);
  interrupt_state interrupt_state_1 (
    .CLK(CLK), .Op_code(Op_code), .keyboard_out(keyboard1_out),
    .called_interrupted_handler_yet(called_interrupt_handler_yet),
    .resolved_interrupt_handler_yet(resolved_interrupt_handler_yet),
    .interrupted_this_cycle(currently_interrupted), .cur_char(cur_char), .thread_number(thread_number));
  Register_Bank Register_Bank (
    .Op_code(Op_code), .CLK(CLK), .RAM_out(RAM_out), .ALSU_out(ALSU_out), .PC_in(PC_in),
    .CALL_RETURN(CALL_RETURN), .interrupted_and_NOT_called_handler(and_1_out), .R_b(R_b), .R_a(R_a),
    .R_d(R_d), .R0(R0), .R1(R1), .R2(R2), .R3(R3), .R4(R4), .R5(R5), .R6(R6), .R7(R7), .R8(R8), .R9(R9),
    .R10(R10), .R11(R11), .R12(R12), .R13(R13), .R14(R14), .R15(R15));
  Comparator #(.width(4)) comparator_1 (.a(Op_code[15:12]), .b(4'b0010), .eq(comparator_1_eq));  // open: gt, lt
  Comparator #(.width(4)) comparator_2 (.a(Op_code[11:8]), .b(4'b0000), .eq(comparator_2_eq));  // open: gt, lt
  Comparator #(.width(4)) comparator_3 (.a(Op_code[11:8]), .b(4'b0001), .eq(comparator_3_eq));  // open: gt, lt
  // Probe on PC_in
  Counter #(.width(16), .max('hffff)) counter_2 (
    .load(BRANCH_branch), .D(BRANCH_pc_out), .count(not_2_out), .Q(PC_in), .clk(CLK));  // open: carry, clr
  ROM #(.addrWidth(2), .dataWidth(16)) rom_1 (.addr(counter_1_q), .data(CALL_INTERRUPT_OP_code));  // open: sel
  or or_1 (or_1_out, comparator_2_eq, comparator_3_eq);
  and and_2 (CALL_RETURN, comparator_1_eq, or_1_out);
  // Probe on ROM_Op_code
  ROM #(.addrWidth(16), .dataWidth(16)) rom_2 (.addr(PC_in), .data(ROM_Op_code));  // open: sel
  LED u_F0 (.in(F0));
  LED u_F1 (.in(F1));
  LED u_F2 (.in(F2));
  LED u_F3 (.in(F3));
  LED u_F4 (.in(F4));
  RAM ram_1 (.Op_code(Op_code), .R_b(R_b), .RAM_address(ram_1_ram_address), .load(load), .load_store(load_store));
  and and_3 (and_3_out, ~called_interrupt_handler_yet, currently_interrupted);  // AND_Gate
  // Probe on R0
  // Probe on R4
  // Probe on R8
  // Probe on R12
  BitSelector #(.width(16), .group(7)) bitselector_1 (.in(R_d), .out(char_out), .sel(2'b00));
  BitSelector #(.width(16)) bitselector_2 (.in(R_a), .out(keyboard_to_read_from), .sel(4'b0000));
  Flag_Bank Flag_Bank (
    .CLK(CLK), .Op_code(Op_code), .R_d(R_d), .ALSU_out(ALSU_out), .ALSU_overflow(ALSU_overflow),
    .ALSU_carry_out(ALSU_carry_out), .RAM_out(RAM_out), .F0(F0), .F1(F1), .F2(F2), .F3(F3), .F4(F4));
  Multiplexer #(.width(16)) multiplexer_1 (
    .in0(ROM_Op_code), .in1(CALL_INTERRUPT_OP_code), .out(Op_code), .sel(and_3_out));  // open: en
  // Probe on R1
  // Probe on R5
  // Probe on R9
  // Probe on R13
  ALSU ALSU (
    .Op_code(Op_code), .R_b(R_b), .R_a(R_a), .R_d(R_d), .F0(F0), .F1(F1), .F2(F2), .F3(F3), .F4(F4),
    .cur_char(cur_char), .thread_number(thread_number), .ALSU_out(ALSU_out), .ALSU_overflow(ALSU_overflow),
    .ALSU_carry_out(ALSU_carry_out));
  RAM_part #(.addrWidth(16), .dataWidth(16)) ram_2 (
    .addr(ram_1_ram_address), .data(RAM_out), .sel(load_store), .clk(CLK), .ld(load));  // open: clr
  // Probe on R2
  // Probe on R6
  // Probe on R10
  // Probe on R14
  not not_3 (not_3_out, load);
  assign RAM_out = not_3_out ? R_d : 16'bz;  // Controlled_Buffer controlled_buffer_1
  // Probe on R3
  // Probe on R7
  // Probe on R11
  // Probe on R15

  assign screen_number = keyboard_to_read_from;

  // Other names for the same wires on the sheet: interrupted_this_cycle = currently_interrupted;
  //   _0_3[3:0] = Op_code[3:0]; _4_7[3:0] = Op_code[7:4]; _8_11[3:0] = Op_code[11:8]; Op[3:0] = Op_code[15:12]

  // Notes on the sheet:
  //   put_char: 0001 (reg with char) (reg with screen #) 0000
  //   get_char: 0001 (reg to place char in) (reg with kb to read from) 0001
  //   contents of rom_1 (hex, n*v repeats v):
  //   ed08 fd00 20cd
  //   contents of rom_2 (hex, n*v repeats v):
  //   3160 ea01 fac0 709a e101 f100 3180 ff 6d0e 6c1e ea01 fac0 610a 621a 632a 643a 654a 665a 676a 687a
  //   698a 6a9a 6baa 6cba 6dca 6eda 6fea 3470 64fa 1321 3068 b030 805 ed96 fd00 20cd 4 ed3f fd00 20cd ea01
  //   fac0 44fa 3478 410a 421a 432a 443a 454a 465a 476a 487a 498a 4a9a 4baa 4cba 4dca 4eda 4fea 4d0e 4c1e
  //   2400 21cd 6d2e 6c3e 1112 3121 44f1 3478 4211 4321 4431 4541 4651 4761 4871 4981 4a91 4ba1 4cb1 4dc1
  //   4ed1 4fe1 4101 e621 f600 a556 e201 f200 e154 f100 1120 e168 f100 1120 e172 f100 1120 e165 f100 1120
  //   e161 f100 1120 e164 f100 1120 e120 f100 1120 1112 31af 1120 e120 f100 7*1120 1520 3580 b556 e10a
  //   f100 1120 1a12 3a2a 610a 621a 632a 643a 654a 665a 676a 687a 698a 6a9a 6baa 6cba 6dca 6eda 6fea 3470
  //   64fa 4d2e 4c3e 21cd ea01 fac0 e201 f200 1321 e50a f500 3068 b035 809 579a 3780 779a a90a 3998 a979
  //   6309 10 579a a90a 3999 e201 f200 4309 1320 6009 3980 37c0 3068 b070 5f9 1520 709a 21cd
  //   sign
  //   zero
  //   overflow
  //   carry
  //   block
endmodule

module Register_Bank (
  input  [15:0] Op_code,
  input  CLK,
  input  [15:0] RAM_out,
  input  [15:0] ALSU_out,
  input  [15:0] PC_in,
  input  CALL_RETURN,
  input  interrupted_and_NOT_called_handler,
  output [15:0] R_b,
  output [15:0] R_a,
  output [15:0] R_d,
  output [15:0] R0,
  output [15:0] R1,
  output [15:0] R2,
  output [15:0] R3,
  output [15:0] R4,
  output [15:0] R5,
  output [15:0] R6,
  output [15:0] R7,
  output [15:0] R8,
  output [15:0] R9,
  output [15:0] R10,
  output [15:0] R11,
  output [15:0] R12,
  output [15:0] R13,
  output [15:0] R14,
  output [15:0] R15
);

  wire ALSU_op, and_1_out, and_2_out, and_3_out, ARITH_LOGICAL_SHIFT_SET, comparator_1_gt, comparator_2_eq,
       comparator_2_lt, comparator_3_eq, comparator_4_gt, comparator_5_eq, comparator_5_gt, comparator_6_lt,
       comparator_7_eq, comparator_8_eq, comparator_9_eq, comparator_10_gt, comparator_11_eq,
       comparator_12_gt, comparator_13_lt, comparator_14_eq, comparator_15_eq, comparator_16_eq, GET_CHAR,
       GET_THREAD_NUMBER, LOAD, multiplexer_2_out, or_1_out, or_3_out, R0_en, R1_en, R2_en, R3_en, R4_en,
       R5_en, R6_en, R7_en, R8_en, R9_en, R10_en, R11_en, R12_en, R12_enable, R13_en, R13_enable, R14_en,
       R14_enable, R15_en, SAVEF, WRITE;
  wire [15:0] adder_1_out, data_to_write, multiplexer_4_out, R12_new, R13_new, R14_new;

  Adder #(.width(16)) adder_1 (.a(PC_in), .b(16'h1), .out(adder_1_out));  // open: cin, cout
  Multiplexer #(.width(16)) multiplexer_1 (
    .in0(RAM_out), .in1(ALSU_out), .out(data_to_write), .sel(ALSU_op));  // open: en
  Multiplexer multiplexer_2 (.in0(1'b0), .in1(1'b1), .out(multiplexer_2_out), .sel(WRITE));  // open: en
  Demultiplexer #(.select(4)) demultiplexer_1 (
    .out0(R0_en), .out1(R1_en), .out2(R2_en), .out3(R3_en), .out4(R4_en), .out5(R5_en), .out6(R6_en),
    .out7(R7_en), .out8(R8_en), .out9(R9_en), .out10(R10_en), .out11(R11_en), .out12(R12_enable),
    .out13(R13_enable), .out14(R14_enable), .out15(R15_en), .in(multiplexer_2_out), .sel(Op_code[11:8]));  // open: en
  Multiplexer #(.select(4), .width(16)) multiplexer_3 (
    .in0(R0), .in1(R1), .in2(R2), .in3(R3), .in4(R4), .in5(R5), .in6(R6), .in7(R7), .in8(R8), .in9(R9),
    .in10(R10), .in11(R11), .in12(R12), .in13(R13), .in14(R14), .in15(R15), .out(R_b), .sel(Op_code[3:0]));  // open: en
  Multiplexer #(.width(16)) multiplexer_4 (
    .in0(adder_1_out), .in1(PC_in), .out(multiplexer_4_out), .sel(interrupted_and_NOT_called_handler));  // open: en
  Comparator #(.width(4), .mode("unsigned")) comparator_1 (
    .a(Op_code[15:12]), .b(4'b0111), .gt(comparator_1_gt));  // open: eq, lt
  Comparator #(.width(4), .mode("unsigned")) comparator_2 (
    .a(Op_code[15:12]), .b(4'b1111), .eq(comparator_2_eq), .lt(comparator_2_lt));  // open: gt
  Comparator #(.width(4), .mode("unsigned")) comparator_3 (
    .a(Op_code[15:12]), .b(4'b0011), .eq(comparator_3_eq));  // open: gt, lt
  or or_1 (or_1_out, comparator_2_eq, comparator_2_lt);
  Comparator #(.width(4), .mode("unsigned")) comparator_4 (
    .a(Op_code[7:4]), .b(4'b0111), .gt(comparator_4_gt));  // open: eq, lt
  Comparator #(.width(4), .mode("unsigned")) comparator_5 (
    .a(Op_code[7:4]), .b(4'b0000), .gt(comparator_5_gt), .eq(comparator_5_eq));  // open: lt
  Comparator #(.width(4), .mode("unsigned")) comparator_6 (
    .a(Op_code[7:4]), .b(4'b0110), .lt(comparator_6_lt));  // open: gt, eq
  Comparator #(.width(4), .mode("unsigned")) comparator_7 (
    .a(Op_code[7:4]), .b(4'b0111), .eq(comparator_7_eq));  // open: gt, lt
  Comparator #(.width(4), .mode("unsigned")) comparator_8 (
    .a(Op_code[3:0]), .b(4'b0000), .eq(comparator_8_eq));  // open: gt, lt
  or or_2 (ALSU_op, ARITH_LOGICAL_SHIFT_SET, SAVEF, GET_CHAR, GET_THREAD_NUMBER);
  Multiplexer #(.width(16)) multiplexer_5 (
    .in0(data_to_write), .in1(R14), .out(R12_new), .sel(CALL_RETURN));  // open: en
  Multiplexer #(.width(16)) multiplexer_6 (
    .in0(data_to_write), .in1(R12), .out(R14_new), .sel(CALL_RETURN));  // open: en
  Multiplexer #(.width(16)) multiplexer_7 (
    .in0(data_to_write), .in1(multiplexer_4_out), .out(R13_new), .sel(CALL_RETURN));  // open: en
  Multiplexer #(.select(4), .width(16)) multiplexer_8 (
    .in0(R0), .in1(R1), .in2(R2), .in3(R3), .in4(R4), .in5(R5), .in6(R6), .in7(R7), .in8(R8), .in9(R9),
    .in10(R10), .in11(R11), .in12(R12), .in13(R13), .in14(R14), .in15(R15), .out(R_a), .sel(Op_code[7:4]));  // open: en
  and and_1 (and_1_out, comparator_1_gt, or_1_out);
  and and_2 (and_2_out, comparator_3_eq, comparator_4_gt);
  or or_3 (or_3_out, comparator_5_gt, comparator_5_eq);
  and and_3 (and_3_out, comparator_3_eq, or_3_out, comparator_6_lt);
  and and_4 (SAVEF, comparator_3_eq, comparator_7_eq, comparator_8_eq);
  Register #(.width(16)) u_R0 (.D({16{1'b0}}), .en(R0_en), .Q(R0), .clk(CLK));  // open: clr
  Register #(.width(16)) u_R2 (.D(data_to_write), .en(R2_en), .Q(R2), .clk(CLK));  // open: clr
  Register #(.width(16)) u_R4 (.D(data_to_write), .en(R4_en), .Q(R4), .clk(CLK));  // open: clr
  Register #(.width(16)) u_R6 (.D(data_to_write), .en(R6_en), .Q(R6), .clk(CLK));  // open: clr
  Register #(.width(16)) u_R8 (.D(data_to_write), .en(R8_en), .Q(R8), .clk(CLK));  // open: clr
  Register #(.width(16)) u_R10 (.D(data_to_write), .en(R10_en), .Q(R10), .clk(CLK));  // open: clr
  Register #(.width(16)) u_R12 (.D(R12_new), .en(R12_en), .Q(R12), .clk(CLK));  // open: clr
  Register #(.width(16)) u_R14 (.D(R14_new), .en(R14_en), .Q(R14), .clk(CLK));  // open: clr
  or or_4 (ARITH_LOGICAL_SHIFT_SET, and_1_out, and_2_out, and_3_out);
  or or_5 (WRITE, ALSU_op, LOAD);
  Multiplexer #(.select(4), .width(16)) multiplexer_9 (
    .in0(R0), .in1(R1), .in2(R2), .in3(R3), .in4(R4), .in5(R5), .in6(R6), .in7(R7), .in8(R8), .in9(R9),
    .in10(R10), .in11(R11), .in12(R12), .in13(R13), .in14(R14), .in15(R15), .out(R_d), .sel(Op_code[11:8]));  // open: en
  Register #(.width(16)) u_R1 (.D(data_to_write), .en(R1_en), .Q(R1), .clk(CLK));  // open: clr
  Register #(.width(16)) u_R3 (.D(data_to_write), .en(R3_en), .Q(R3), .clk(CLK));  // open: clr
  Register #(.width(16)) u_R5 (.D(data_to_write), .en(R5_en), .Q(R5), .clk(CLK));  // open: clr
  Register #(.width(16)) u_R7 (.D(data_to_write), .en(R7_en), .Q(R7), .clk(CLK));  // open: clr
  Register #(.width(16)) u_R9 (.D(data_to_write), .en(R9_en), .Q(R9), .clk(CLK));  // open: clr
  Register #(.width(16)) u_R11 (.D(data_to_write), .en(R11_en), .Q(R11), .clk(CLK));  // open: clr
  Register #(.width(16)) u_R13 (.D(R13_new), .en(R13_en), .Q(R13), .clk(CLK));  // open: clr
  Register #(.width(16)) u_R15 (.D(data_to_write), .en(R15_en), .Q(R15), .clk(CLK));  // open: clr
  Comparator #(.width(4)) comparator_9 (.a(Op_code[15:12]), .b(4'b0001), .eq(comparator_9_eq));  // open: gt, lt
  Comparator #(.width(4)) comparator_10 (.a(Op_code[7:4]), .b(4'b0000), .gt(comparator_10_gt));  // open: eq, lt
  Comparator #(.width(4)) comparator_11 (.a(Op_code[3:0]), .b(4'b0001), .eq(comparator_11_eq));  // open: gt, lt
  Comparator #(.width(4), .mode("unsigned")) comparator_12 (
    .a(Op_code[15:12]), .b(4'b0011), .gt(comparator_12_gt));  // open: eq, lt
  Comparator #(.width(4), .mode("unsigned")) comparator_13 (
    .a(Op_code[15:12]), .b(4'b0110), .lt(comparator_13_lt));  // open: gt, eq
  and and_5 (GET_CHAR, comparator_9_eq, comparator_10_gt, comparator_11_eq);
  and and_6 (LOAD, comparator_12_gt, comparator_13_lt);
  Multiplexer multiplexer_10 (.in0(R12_enable), .in1(1'b1), .out(R12_en), .sel(CALL_RETURN));  // open: en
  Multiplexer multiplexer_11 (.in0(R14_enable), .in1(1'b1), .out(R14_en), .sel(CALL_RETURN));  // open: en
  Multiplexer multiplexer_12 (.in0(R13_enable), .in1(1'b1), .out(R13_en), .sel(CALL_RETURN));  // open: en
  Comparator #(.width(4)) comparator_14 (.a(Op_code[15:12]), .b(4'b0001), .eq(comparator_14_eq));  // open: gt, lt
  Comparator #(.width(4)) comparator_15 (.a(Op_code[7:4]), .b(4'b0001), .eq(comparator_15_eq));  // open: gt, lt
  Comparator #(.width(4)) comparator_16 (.a(Op_code[3:0]), .b(4'b0010), .eq(comparator_16_eq));  // open: gt, lt
  and and_7 (GET_THREAD_NUMBER, comparator_14_eq, comparator_15_eq, comparator_16_eq);

  // Other names for the same wires on the sheet: R1_new[15:0] = data_to_write; R2_new[15:0] = data_to_write;
  //   R3_new[15:0] = data_to_write; R4_new[15:0] = data_to_write; R5_new[15:0] = data_to_write;
  //   R6_new[15:0] = data_to_write; R7_new[15:0] = data_to_write; R8_new[15:0] = data_to_write;
  //   R9_new[15:0] = data_to_write; R10_new[15:0] = data_to_write; R11_new[15:0] = data_to_write;
  //   R15_new[15:0] = data_to_write; b[3:0] = Op_code[3:0]; a[3:0] = Op_code[7:4]; d[3:0] = Op_code[11:8];
  //   _9_15[6:0] = Op_code[15:9]; Op[3:0] = Op_code[15:12]; R0_enable = R0_en; R0_out[15:0] = R0; R1_enable = R1_en;
  //   R1_out[15:0] = R1; R2_enable = R2_en; R2_out[15:0] = R2; R3_enable = R3_en; R3_out[15:0] = R3;
  //   R4_enable = R4_en; R4_out[15:0] = R4; R5_enable = R5_en; R5_out[15:0] = R5; R6_enable = R6_en;
  //   R6_out[15:0] = R6; R7_enable = R7_en; R7_out[15:0] = R7; R8_enable = R8_en; R8_out[15:0] = R8;
  //   R9_enable = R9_en; R9_out[15:0] = R9; R10_enable = R10_en; R10_out[15:0] = R10; R11_enable = R11_en;
  //   R11_out[15:0] = R11; R12_out[15:0] = R12; R13_out[15:0] = R13; R14_out[15:0] = R14; R15_enable = R15_en;
  //   R15_out[15:0] = R15

  // Notes on the sheet:
  //   If ADD/SUB/MUL/SHIFT/SET
  //   If INC/DEC
  //   If SHIFT
  //   If SAVEF
endmodule

module Flag_Bank (
  input  CLK,
  input  [15:0] Op_code,
  input  [15:0] R_d,
  input  [15:0] ALSU_out,
  input  ALSU_overflow,
  input  ALSU_carry_out,
  input  [15:0] RAM_out,
  output F0,
  output F1,
  output F2,
  output F3,
  output F4
);

  wire F0_in, F1_in, F2_in, F3_in, F4_in;

  D_Flip_Flop u_F0 (.clk(CLK), .D(F0_in), .Q(F0));  // open: Qn, preset, en, reset
  D_Flip_Flop u_F1 (.clk(CLK), .D(F1_in), .Q(F1));  // open: Qn, preset, en, reset
  D_Flip_Flop u_F2 (.clk(CLK), .D(F2_in), .Q(F2));  // open: Qn, preset, en, reset
  D_Flip_Flop u_F3 (.clk(CLK), .D(F3_in), .Q(F3));  // open: Qn, preset, en, reset
  D_Flip_Flop u_F4 (.clk(CLK), .D(F4_in), .Q(F4));  // open: Qn, preset, en, reset
  update_flags update_flags (
    .Op_code(Op_code), .R_d(R_d), .R_data_out(ALSU_out), .ALSU_overflow(ALSU_overflow),
    .ALSU_carry_out(ALSU_carry_out), .F0(F0), .F1(F1), .F2(F2), .F3(F3), .F4(F4), .RAM_out(RAM_out),
    .F0_out(F0_in), .F1_out(F1_in), .F2_out(F2_in), .F3_out(F3_in), .F4_out(F4_in));
endmodule

module ALSU (
  input  [15:0] Op_code,
  input  [15:0] R_b,
  input  [15:0] R_a,
  input  [15:0] R_d,
  input  F0,
  input  F1,
  input  F2,
  input  F3,
  input  F4,
  input  [6:0] cur_char,
  input  [2:0] thread_number,
  output [15:0] ALSU_out,
  output ALSU_overflow,
  output ALSU_carry_out
);

  wire _6_6, _7_7, ADD_carry_out, ADD_overflow_out, and_2_out, ARITH, ASL, ASL_carry_out, ASL_overflow_out,
       ASR_carry_out, bitselector_8_out, bitselector_10_out, comparator_1_eq, comparator_2_gt,
       comparator_3_gt, comparator_4_lt, comparator_5_eq, comparator_6_eq, DEC_carry_out, DEC_overflow_out,
       INC_carry_out, INC_DEC, INC_overflow_out, LSL_carry_out, LSR_carry_out, MUL_carry_out,
       MUL_overflow_out, multiplexer_1_out, multiplexer_2_out, multiplexer_3_out, multiplexer_5_out,
       multiplexer_6_out, multiplexer_9_out, multiplexer_10_out, SUB_carry_out, SUB_overflow_out;
  wire [1:0] bitselector_7_out, bitselector_9_out, bitselector_11_out;
  wire [2:0] _4_6, _9_11;
  wire [3:0] shifter_1_out;
  wire [5:0] _0_5;
  wire [7:0] _0_7;
  wire [15:0] _1, _3, _6, _8, _9, A, ASL_data_out, ASR_data_out, B, C, cur_char_16_bit, D, DEC_data_out, E,
       F, INC_data_out, LSL8_data_out, LSL_data_out, LSR8_data_out, LSR_data_out, multiplexer_4_out,
       multiplexer_8_out, SAVEF_data_out, thread_number_16_bit;

  BitSelector #(.width(16), .group(8)) bitselector_1 (.in(Op_code), .out(_0_7), .sel(1'b0));
  BitSelector #(.width(16), .group(6)) bitselector_2 (.in(Op_code), .out(_0_5), .sel(2'b00));
  BitSelector #(.width(16)) bitselector_3 (.in(Op_code), .out(_6_6), .sel(4'b0110));
  BitSelector #(.width(16)) bitselector_4 (.in(Op_code), .out(_7_7), .sel(4'b0111));
  BitSelector #(.width(4), .group(3)) bitselector_5 (.in(Op_code[7:4]), .out(_4_6), .sel(1'b0));
  BitSelector #(.width(4), .group(3)) bitselector_6 (.in(shifter_1_out), .out(_9_11), .sel(1'b0));
  Shifter #(.width(4), .shift("lr")) shifter_1 (.in(Op_code[11:8]), .\dist (2'b01), .out(shifter_1_out));
  LSL LSL (.R_b(R_b), .F3(F3), .F4(F4), .data_out(LSL_data_out), .carry_out(LSL_carry_out));
  LSR LSR (.R_b(R_b), .F3(F3), .F4(F4), .data_out(LSR_data_out), .carry_out(LSR_carry_out));
  LSL8 LSL8 (.R_b(R_b), .data_out(LSL8_data_out));
  LSR8 LSR8 (.R_b(R_b), .data_out(LSR8_data_out));
  ASL u_ASL (
    .R_b(R_b), .F3(F3), .F4(F4), .data_out(ASL_data_out), .carry_out(ASL_carry_out),
    .overflow_out(ASL_overflow_out));
  ASR ASR (.R_b(R_b), .data_out(ASR_data_out), .carry_out(ASR_carry_out));
  SAVEF SAVEF (.F0(F0), .F1(F1), .F2(F2), .F3(F3), .F4(F4), .data_out(SAVEF_data_out));
  BitSelector #(.width(4), .group(2)) bitselector_7 (.in(Op_code[15:12]), .out(bitselector_7_out), .sel(1'b0));
  BitSelector #(.width(4)) bitselector_8 (.in(Op_code[7:4]), .out(bitselector_8_out), .sel(2'b10));
  assign cur_char_16_bit = {{9{1'b0}}, cur_char};  // Bit_Extender bit_extender_1
  assign thread_number_16_bit = {{13{1'b0}}, thread_number};  // Bit_Extender bit_extender_2
  INC INC (
    .R_d(R_d), .Epsilon(_0_5), .data_out(INC_data_out), .carry_out(INC_carry_out),
    .overflow_out(INC_overflow_out));
  DEC DEC (
    .R_d(R_d), .Epsilon(_0_5), .data_out(DEC_data_out), .carry_out(DEC_carry_out),
    .overflow_out(DEC_overflow_out));
  Multiplexer #(.select(2)) multiplexer_1 (
    .in0(MUL_overflow_out), .in1(1'b0), .in2(ADD_overflow_out), .in3(SUB_overflow_out),
    .out(multiplexer_1_out), .sel(bitselector_7_out));  // open: en
  Multiplexer multiplexer_2 (
    .in0(INC_overflow_out), .in1(DEC_overflow_out), .out(multiplexer_2_out), .sel(bitselector_8_out));  // open: en
  BitSelector #(.width(4), .group(2)) bitselector_9 (.in(Op_code[15:12]), .out(bitselector_9_out), .sel(1'b0));
  Multiplexer multiplexer_3 (
    .in0(INC_carry_out), .in1(DEC_carry_out), .out(multiplexer_3_out), .sel(bitselector_10_out));  // open: en
  BitSelector #(.width(4)) bitselector_10 (.in(Op_code[7:4]), .out(bitselector_10_out), .sel(2'b10));
  Comparator #(.width(4), .mode("unsigned")) comparator_1 (
    .a(Op_code[15:12]), .b(4'b0011), .eq(comparator_1_eq));  // open: gt, lt
  Comparator #(.width(4), .mode("unsigned")) comparator_2 (
    .a(Op_code[7:4]), .b(4'b0111), .gt(comparator_2_gt));  // open: eq, lt
  Comparator #(.width(4), .mode("unsigned")) comparator_3 (
    .a(Op_code[15:12]), .b(4'b1001), .gt(comparator_3_gt));  // open: eq, lt
  Comparator #(.width(4), .mode("unsigned")) comparator_4 (
    .a(Op_code[15:12]), .b(4'b1101), .lt(comparator_4_lt));  // open: gt, eq
  Comparator #(.width(4), .mode("unsigned")) comparator_5 (
    .a(Op_code[15:12]), .b(4'b0011), .eq(comparator_5_eq));  // open: gt, lt
  Comparator #(.width(4), .mode("unsigned")) comparator_6 (
    .a(Op_code[7:4]), .b(4'b0100), .eq(comparator_6_eq));  // open: gt, lt
  Multiplexer #(.select(3), .width(16)) multiplexer_4 (
    .in0(LSL_data_out), .in1(LSR_data_out), .in2(LSL8_data_out), .in3(LSR8_data_out), .in4(ASL_data_out),
    .in5(ASR_data_out), .in7(SAVEF_data_out), .out(multiplexer_4_out), .sel(_4_6));  // open: in6, en
  Multiplexer multiplexer_5 (
    .in0(multiplexer_1_out), .in1(multiplexer_2_out), .out(multiplexer_5_out), .sel(INC_DEC));  // open: en
  Multiplexer #(.select(2)) multiplexer_6 (
    .in0(MUL_carry_out), .in1(1'b0), .in2(ADD_carry_out), .in3(SUB_carry_out), .out(multiplexer_6_out),
    .sel(bitselector_9_out));  // open: en
  and and_1 (INC_DEC, comparator_1_eq, comparator_2_gt);
  and and_2 (and_2_out, comparator_3_gt, comparator_4_lt);
  and and_3 (ASL, comparator_5_eq, comparator_6_eq);
  Multiplexer #(.width(16)) multiplexer_7 (
    .in0(multiplexer_4_out), .in1(multiplexer_8_out), .out(_3), .sel(_7_7));  // open: en
  Multiplexer #(.width(16)) multiplexer_8 (
    .in0(INC_data_out), .in1(DEC_data_out), .out(multiplexer_8_out), .sel(_6_6));  // open: en
  Multiplexer #(.select(2)) multiplexer_9 (
    .in0(LSL_carry_out), .in1(LSR_carry_out), .in2(ASL_carry_out), .in3(ASR_carry_out),
    .out(multiplexer_9_out), .sel({Op_code[6], Op_code[4]}));  // open: en
  Multiplexer multiplexer_10 (
    .in0(multiplexer_6_out), .in1(multiplexer_3_out), .out(multiplexer_10_out), .sel(INC_DEC));  // open: en
  or or_1 (ARITH, and_2_out, INC_DEC);
  Multiplexer #(.select(4), .width(16)) multiplexer_11 (
    .in0({16{1'b0}}), .in1(_1), .in2({16{1'b0}}), .in3(_3), .in4({16{1'b0}}), .in5({16{1'b0}}), .in6(_6),
    .in7({16{1'b0}}), .in8(_8), .in9(_9), .in10(A), .in11(B), .in12(C), .in13(D), .in14(E), .in15(F),
    .out(ALSU_out), .sel(Op_code[15:12]));  // open: en
  Multiplexer multiplexer_12 (
    .in0(multiplexer_5_out), .in1(ASL_overflow_out), .out(ALSU_overflow), .sel(ASL));  // open: en
  Multiplexer multiplexer_13 (
    .in0(multiplexer_9_out), .in1(multiplexer_10_out), .out(ALSU_carry_out), .sel(ARITH));  // open: en
  Multiplexer #(.select(2), .width(16)) multiplexer_14 (
    .in0({16{1'b0}}), .in1(cur_char_16_bit), .in2(thread_number_16_bit), .in3({16{1'b0}}), .out(_1),
    .sel(bitselector_11_out));  // open: en
  BitSelector #(.width(4), .group(2)) bitselector_11 (.in(Op_code[3:0]), .out(bitselector_11_out), .sel(1'b0));
  AND AND_4 (.R_b(R_b), .R_a(R_a), .data_out(_8));
  OR OR_2 (.R_b(R_b), .R_a(R_a), .data_out(_9));
  ADD ADD (
    .R_b(R_b), .R_a(R_a), .F3(F3), .F4(F4), .data_out(A), .carry_out(ADD_carry_out),
    .overflow_out(ADD_overflow_out));
  SUB SUB (
    .R_b(R_b), .R_a(R_a), .F3(F3), .F4(F4), .data_out(B), .carry_out(SUB_carry_out),
    .overflow_out(SUB_overflow_out));
  MUL MUL (.R_b(R_b), .R_a(R_a), .data_out(C), .carry_out(MUL_carry_out), .overflow_out(MUL_overflow_out));
  XOR XOR (.R_b(R_b), .R_a(R_a), .data_out(D));
  SETLO SETLO (.v(_0_7), .data_out(E));
  SETHI SETHI (.v(_0_7), .R_d(R_d), .data_out(F));

  // Other names for the same wires on the sheet: ARITH_SHIFT_carry_out = ALSU_carry_out;
  //   ARITH_SHIFT_overflow = ALSU_overflow; _0_3[3:0] = Op_code[3:0]; _4_7[3:0] = Op_code[7:4];
  //   _8_11[3:0] = Op_code[11:8]; Op[3:0] = Op_code[15:12]

  // Notes on the sheet:
  //   If INC/DEC
  //   If ADD/SUB/MUL or INC/DEC
endmodule

module ADD (
  input  [15:0] R_b,
  input  [15:0] R_a,
  input  F3,
  input  F4,
  output [15:0] data_out,
  output carry_out,
  output overflow_out
);

  wire adder_1_cout, adder_2_cout, and_2_out, and_3_out, bitselector_1_out, bitselector_2_out,
       bitselector_3_out, bitselector_4_out, bitselector_5_out, bitselector_6_out, c_and_cb_prime;
  wire [15:0] adder_1_out, bit_extender_1_out;

  and and_1 (c_and_cb_prime, F3, ~F4);  // AND_Gate
  BitSelector #(.width(16)) bitselector_1 (.in(R_b), .out(bitselector_1_out), .sel(4'b1111));
  and and_2 (and_2_out, ~bitselector_1_out, ~bitselector_2_out, bitselector_3_out);  // AND_Gate
  BitSelector #(.width(16)) bitselector_2 (.in(R_a), .out(bitselector_2_out), .sel(4'b1111));
  BitSelector #(.width(16)) bitselector_3 (.in(data_out), .out(bitselector_3_out), .sel(4'b1111));
  BitSelector #(.width(16)) bitselector_4 (.in(R_b), .out(bitselector_4_out), .sel(4'b1111));
  BitSelector #(.width(16)) bitselector_5 (.in(R_a), .out(bitselector_5_out), .sel(4'b1111));
  and and_3 (and_3_out, bitselector_4_out, bitselector_5_out, ~bitselector_6_out);  // AND_Gate
  BitSelector #(.width(16)) bitselector_6 (.in(data_out), .out(bitselector_6_out), .sel(4'b1111));
  Adder #(.width(16)) adder_1 (.a(R_b), .b(R_a), .out(adder_1_out), .cout(adder_1_cout));  // open: cin
  or or_1 (overflow_out, and_2_out, and_3_out);
  assign bit_extender_1_out = {{15{1'b0}}, c_and_cb_prime};  // Bit_Extender bit_extender_1
  Adder #(.width(16)) adder_2 (
    .a(adder_1_out), .b(bit_extender_1_out), .out(data_out), .cout(adder_2_cout));  // open: cin
  or or_2 (carry_out, adder_2_cout, adder_1_cout);

  // Notes on the sheet:
  //   P + P = N
  //   N + N = P
  //   Cases for overflow for adding
  //   1. Adding 2 positives and getting a negative
  //   2. Adding 2 negatives and getting a positive
endmodule

module SUB (
  input  [15:0] R_b,
  input  [15:0] R_a,
  input  F3,
  input  F4,
  output [15:0] data_out,
  output carry_out,
  output overflow_out
);

  wire and_2_out, and_3_out, bitselector_1_out, bitselector_2_out, bitselector_3_out, bitselector_4_out,
       bitselector_5_out, bitselector_6_out, c_prime_and_cb_prime, comparator_1_lt;
  wire [15:0] bit_extender_1_out, subtractor_1_out;

  and and_1 (c_prime_and_cb_prime, ~F3, ~F4);  // AND_Gate
  BitSelector #(.width(16)) bitselector_1 (.in(R_a), .out(bitselector_1_out), .sel(4'b1111));
  BitSelector #(.width(16)) bitselector_2 (.in(R_b), .out(bitselector_2_out), .sel(4'b1111));
  BitSelector #(.width(16)) bitselector_3 (.in(data_out), .out(bitselector_3_out), .sel(4'b1111));
  BitSelector #(.width(16)) bitselector_4 (.in(R_a), .out(bitselector_4_out), .sel(4'b1111));
  BitSelector #(.width(16)) bitselector_5 (.in(R_b), .out(bitselector_5_out), .sel(4'b1111));
  BitSelector #(.width(16)) bitselector_6 (.in(data_out), .out(bitselector_6_out), .sel(4'b1111));
  Subtractor #(.width(16)) subtractor_1 (.a(R_a), .b(R_b), .out(subtractor_1_out));  // open: bin, bout
  and and_2 (and_2_out, ~bitselector_1_out, bitselector_2_out, bitselector_3_out);  // AND_Gate
  and and_3 (and_3_out, bitselector_4_out, ~bitselector_5_out, ~bitselector_6_out);  // AND_Gate
  assign bit_extender_1_out = {{15{1'b0}}, c_prime_and_cb_prime};  // Bit_Extender bit_extender_1
  Comparator #(.width(16), .mode("unsigned")) comparator_1 (.a(R_a), .b(R_b), .lt(comparator_1_lt));  // open: gt, eq
  not not_1 (carry_out, comparator_1_lt);
  or or_1 (overflow_out, and_2_out, and_3_out);
  Subtractor #(.width(16)) subtractor_2 (
    .a(subtractor_1_out), .b(bit_extender_1_out), .out(data_out));  // open: bin, bout

  // Notes on the sheet:
  //   P - N = N
  //   N - P = P
  //   Cases for overflow for subtracting
  //   2. Negative minus positive getting a positive
  //   1. Positive minus negative and getting a negative
endmodule

module MUL (
  input  [15:0] R_b,
  input  [15:0] R_a,
  output [15:0] data_out,
  output carry_out,
  output overflow_out
);

  wire A_0_B_0, A_0_B__0, A__0_B_0, A__0_B__0, comparator_5_eq;
  wire [1:0] sign_A_sign_B;
  wire [3:0] bitfinder_1_index, bitfinder_2_index, bitfinder_3_index, bitfinder_4_index, bitfinder_5_index,
       bitfinder_6_index, bitfinder_7_index, bitfinder_8_index;
  wire [4:0] adder_1_out, adder_2_out, adder_3_out, adder_4_out, bit_extender_1_out, bit_extender_2_out,
       bit_extender_3_out, bit_extender_4_out, bit_extender_5_out, bit_extender_6_out, bit_extender_7_out,
       bit_extender_8_out;
  wire [15:0] multiplier_1_cout;

  BitSelector #(.width(16)) bitselector_1 (.in(R_b), .out(sign_A_sign_B[0]), .sel(4'b1111));
  BitSelector #(.width(16)) bitselector_2 (.in(R_a), .out(sign_A_sign_B[1]), .sel(4'b1111));
  BitFinder #(.width(16), .\type ("high1")) bitfinder_1 (.in(R_b), .index(bitfinder_1_index));  // open: found
  BitFinder #(.width(16), .\type ("high1")) bitfinder_2 (.in(R_a), .index(bitfinder_2_index));  // open: found
  BitFinder #(.width(16), .\type ("high0")) bitfinder_3 (.in(R_b), .index(bitfinder_3_index));  // open: found
  BitFinder #(.width(16), .\type ("high1")) bitfinder_4 (.in(R_a), .index(bitfinder_4_index));  // open: found
  BitFinder #(.width(16), .\type ("high1")) bitfinder_5 (.in(R_b), .index(bitfinder_5_index));  // open: found
  BitFinder #(.width(16), .\type ("high0")) bitfinder_6 (.in(R_a), .index(bitfinder_6_index));  // open: found
  BitFinder #(.width(16), .\type ("high0")) bitfinder_7 (.in(R_b), .index(bitfinder_7_index));  // open: found
  BitFinder #(.width(16), .\type ("high0")) bitfinder_8 (.in(R_a), .index(bitfinder_8_index));  // open: found
  Multiplier #(.width(16)) multiplier_1 (.a(R_b), .b(R_a), .out(data_out), .cout(multiplier_1_cout));  // open: cin
  assign bit_extender_1_out = {{1{1'b0}}, bitfinder_1_index};  // Bit_Extender bit_extender_1
  assign bit_extender_2_out = {{1{1'b0}}, bitfinder_2_index};  // Bit_Extender bit_extender_2
  assign bit_extender_3_out = {{1{1'b0}}, bitfinder_3_index};  // Bit_Extender bit_extender_3
  assign bit_extender_4_out = {{1{1'b0}}, bitfinder_4_index};  // Bit_Extender bit_extender_4
  assign bit_extender_5_out = {{1{1'b0}}, bitfinder_5_index};  // Bit_Extender bit_extender_5
  assign bit_extender_6_out = {{1{1'b0}}, bitfinder_6_index};  // Bit_Extender bit_extender_6
  assign bit_extender_7_out = {{1{1'b0}}, bitfinder_7_index};  // Bit_Extender bit_extender_7
  assign bit_extender_8_out = {{1{1'b0}}, bitfinder_8_index};  // Bit_Extender bit_extender_8
  Adder #(.width(5)) adder_1 (.a(bit_extender_1_out), .b(bit_extender_2_out), .out(adder_1_out));  // open: cin, cout
  Adder #(.width(5)) adder_2 (.a(bit_extender_3_out), .b(bit_extender_4_out), .out(adder_2_out));  // open: cin, cout
  Adder #(.width(5)) adder_3 (.a(bit_extender_5_out), .b(bit_extender_6_out), .out(adder_3_out));  // open: cin, cout
  Adder #(.width(5)) adder_4 (.a(bit_extender_7_out), .b(bit_extender_8_out), .out(adder_4_out));  // open: cin, cout
  Multiplexer #(.select(2)) multiplexer_1 (
    .in0(A__0_B__0), .in1(A__0_B_0), .in2(A_0_B__0), .in3(A_0_B_0), .out(overflow_out), .sel(sign_A_sign_B));  // open: en
  Comparator #(.width(5), .mode("unsigned")) comparator_1 (
    .a(adder_1_out), .b(5'b01110), .gt(A__0_B__0));  // open: eq, lt
  Comparator #(.width(5), .mode("unsigned")) comparator_2 (
    .a(adder_2_out), .b(5'b01110), .gt(A__0_B_0));  // open: eq, lt
  Comparator #(.width(5), .mode("unsigned")) comparator_3 (
    .a(adder_3_out), .b(5'b01110), .gt(A_0_B__0));  // open: eq, lt
  Comparator #(.width(5), .mode("unsigned")) comparator_4 (
    .a(adder_4_out), .b(5'b01110), .gt(A_0_B_0));  // open: eq, lt
  Comparator #(.width(16)) comparator_5 (.a(multiplier_1_cout), .b({16{1'b0}}), .eq(comparator_5_eq));  // open: gt, lt
  not not_1 (carry_out, comparator_5_eq);

  // Notes on the sheet:
  //   4 cases
  //   1. positive times positive
  //   2. positive times negative
  //   3. negative times positive
  //   4. negative times negative
  //   This is because when you multiply, you add the exponents of the 2s
  //   Detect overflow by finding the highest power of 2 in the answer
  //   If the highest power of 2 in the answer is more than 14, then there is overflow
  //   Find the highest power of 2 in the answer by adding the power of the highest power of 2s in the multiplcands
  //   The highest power of 2 in a positive number is the position of the most left 1 in the binary representation
  //   The highest power of 2 in a negative number is the position of the most left 0 in the binary representation
  //   Need to extend the bits before adding the powers because it might overflow
endmodule

module AND (
  input  [15:0] R_b,
  input  [15:0] R_a,
  output [15:0] data_out
);

  assign data_out = R_b & R_a;  // AND_Gate and_1, 16 bits wide
endmodule

module OR (
  input  [15:0] R_b,
  input  [15:0] R_a,
  output [15:0] data_out
);

  assign data_out = R_b | R_a;  // OR_Gate or_1, 16 bits wide
endmodule

module XOR (
  input  [15:0] R_b,
  input  [15:0] R_a,
  output [15:0] data_out
);

  assign data_out = R_b ^ R_a;  // XOR_Gate xor_1, 16 bits wide
endmodule

module SETLO (
  input  [7:0] v,
  output [15:0] data_out
);

  assign data_out = {{8{1'b0}}, v};  // Bit_Extender bit_extender_1
endmodule

module SETHI (
  input  [7:0] v,
  input  [15:0] R_d,
  output [15:0] data_out
);


  assign data_out = {v, R_d[7:0]};
endmodule

module LSL (
  input  [15:0] R_b,
  input  F3,
  input  F4,
  output [15:0] data_out,
  output carry_out
);

  and and_1 (data_out[0], F3, ~F4);  // AND_Gate

  assign carry_out = R_b[15];
  assign data_out[15:1] = R_b[14:0];

  // Other names for the same wires on the sheet: c_and_cb_prime = data_out[0]
endmodule

module LSR (
  input  [15:0] R_b,
  input  F3,
  input  F4,
  output [15:0] data_out,
  output carry_out
);

  and and_1 (data_out[15], F3, ~F4);  // AND_Gate

  assign carry_out = R_b[0];
  assign data_out[14:0] = R_b[15:1];

  // Other names for the same wires on the sheet: c_and_cb_prime = data_out[15]
endmodule

module SAVEF (
  input  F0,
  input  F1,
  input  F2,
  input  F3,
  input  F4,
  output [15:0] data_out
);

  assign data_out = {{11{1'b0}}, {F4, F3, F2, F1, F0}};  // Bit_Extender bit_extender_1
endmodule

module RSTRF (
  input  [15:0] R_d,
  output F0,
  output F1,
  output F2,
  output F3,
  output F4
);


  assign F0 = R_d[0];
  assign F1 = R_d[1];
  assign F2 = R_d[2];
  assign F3 = R_d[3];
  assign F4 = R_d[4];
endmodule

module FON (
  input  F0,
  input  F1,
  input  F2,
  input  F3,
  input  F4,
  input  [15:0] Op_code,
  output F0_out,
  output F1_out,
  output F2_out,
  output F3_out,
  output F4_out
);

  Multiplexer multiplexer_1 (.in0(F0), .in1(1'b1), .out(F0_out), .sel(Op_code[0]));  // open: en
  Multiplexer multiplexer_2 (.in0(F1), .in1(1'b1), .out(F1_out), .sel(Op_code[1]));  // open: en
  Multiplexer multiplexer_3 (.in0(F2), .in1(1'b1), .out(F2_out), .sel(Op_code[2]));  // open: en
  Multiplexer multiplexer_4 (.in0(F3), .in1(1'b1), .out(F3_out), .sel(Op_code[3]));  // open: en
  Multiplexer multiplexer_5 (.in0(F4), .in1(1'b1), .out(F4_out), .sel(Op_code[8]));  // open: en
endmodule

module FOFF (
  input  F0,
  input  F1,
  input  F2,
  input  F3,
  input  F4,
  input  [15:0] Op_code,
  output F0_out,
  output F1_out,
  output F2_out,
  output F3_out,
  output F4_out
);

  Multiplexer multiplexer_1 (.in0(F0), .in1(1'b0), .out(F0_out), .sel(Op_code[0]));  // open: en
  Multiplexer multiplexer_2 (.in0(F1), .in1(1'b0), .out(F1_out), .sel(Op_code[1]));  // open: en
  Multiplexer multiplexer_3 (.in0(F2), .in1(1'b0), .out(F2_out), .sel(Op_code[2]));  // open: en
  Multiplexer multiplexer_4 (.in0(F3), .in1(1'b0), .out(F3_out), .sel(Op_code[3]));  // open: en
  Multiplexer multiplexer_5 (.in0(F4), .in1(1'b0), .out(F4_out), .sel(Op_code[8]));  // open: en
endmodule

module LSL8 (
  input  [15:0] R_b,
  output [15:0] data_out
);


  assign data_out = {R_b[7:0], {8{1'b0}}};
endmodule

module LSR8 (
  input  [15:0] R_b,
  output [15:0] data_out
);


  assign data_out = {{8{1'b0}}, R_b[15:8]};
endmodule

module ASL (
  input  [15:0] R_b,
  input  F3,
  input  F4,
  output [15:0] data_out,
  output carry_out,
  output overflow_out
);

  and and_1 (data_out[0], F3, ~F4);  // AND_Gate

  assign carry_out = R_b[15];
  assign data_out[15:1] = R_b[14:0];
  assign overflow_out = R_b[15];

  // Other names for the same wires on the sheet: c_and_cb_prime = data_out[0]
endmodule

module ASR (
  input  [15:0] R_b,
  output [15:0] data_out,
  output carry_out
);


  assign carry_out = R_b[0];
  assign data_out = {{2{R_b[15]}}, R_b[14:1]};

  // Other names for the same wires on the sheet: _0_0 = R_b[0]
endmodule

module FSET5 (
  input  [15:0] Op_code,
  output F0_out,
  output F1_out,
  output F2_out,
  output F3_out,
  output F4_out
);


  assign F0_out = Op_code[0];
  assign F1_out = Op_code[1];
  assign F2_out = Op_code[2];
  assign F3_out = Op_code[3];
  assign F4_out = Op_code[8];
endmodule

module FSET4 (
  input  [15:0] Op_code,
  output F0_out,
  output F1_out,
  output F2_out,
  output F3_out
);


  assign F0_out = Op_code[0];
  assign F1_out = Op_code[1];
  assign F2_out = Op_code[2];
  assign F3_out = Op_code[3];
endmodule

module INC (
  input  [15:0] R_d,
  input  [5:0] Epsilon,
  output [15:0] data_out,
  output carry_out,
  output overflow_out
);

  wire [15:0] adder_1_out, bit_extender_1_out;

  assign bit_extender_1_out = {{10{1'b0}}, Epsilon};  // Bit_Extender bit_extender_1
  Adder #(.width(16)) adder_1 (.a(bit_extender_1_out), .b(16'h1), .out(adder_1_out));  // open: cin, cout
  ADD add_1 (
    .R_b(R_d), .R_a(adder_1_out), .F3(1'b0), .F4(1'b1), .data_out(data_out), .carry_out(carry_out),
    .overflow_out(overflow_out));
endmodule

module DEC (
  input  [15:0] R_d,
  input  [5:0] Epsilon,
  output [15:0] data_out,
  output carry_out,
  output overflow_out
);

  wire [15:0] adder_1_out, bit_extender_1_out;

  assign bit_extender_1_out = {{10{1'b0}}, Epsilon};  // Bit_Extender bit_extender_1
  Adder #(.width(16)) adder_1 (.a(bit_extender_1_out), .b(16'h1), .out(adder_1_out));  // open: cin, cout
  SUB sub_1 (
    .R_b(adder_1_out), .R_a(R_d), .F3(1'b0), .F4(1'b1), .data_out(data_out), .carry_out(carry_out),
    .overflow_out(overflow_out));
endmodule

module update_F0 (
  input  FON_F0_out,
  input  FSET5_F0_out,
  input  FOFF_F0_out,
  input  FSET4_F0_out,
  input  RSTRF_F0_out,
  input  [2:0] _9_11,
  input  [3:0] _4_7,
  input  [3:0] _0_3,
  input  [15:0] R_d,
  input  F0,
  input  [3:0] Op,
  input  [15:0] RAM_out,
  output F0_out
);

  wire and_1_out, and_2_out, and_3_out, and_4_out, and_5_out, and_6_out, ARITH_LOGICAL_SHIFT,
       bitselector_1_out, bitselector_2_out, comparator_1_gt, comparator_2_lt, comparator_3_eq,
       comparator_4_gt, comparator_5_eq, comparator_5_gt, comparator_6_lt, comparator_7_eq, comparator_8_eq,
       comparator_9_eq, comparator_10_eq, comparator_11_gt, comparator_12_lt, FLAG, load, multiplexer_1_out,
       multiplexer_2_out, multiplexer_3_out, multiplexer_4_out, or_1_out, or_4_out, RSTRF;

  Multiplexer #(.select(3)) multiplexer_1 (
    .in0(FON_F0_out), .in2(FSET5_F0_out), .in4(FOFF_F0_out), .in6(FSET4_F0_out), .out(multiplexer_1_out),
    .sel(_9_11));  // open: in1, in3, in5, in7, en
  Comparator #(.width(4), .mode("unsigned")) comparator_1 (.a(Op), .b(4'b0111), .gt(comparator_1_gt));  // open: eq, lt
  Comparator #(.width(4), .mode("unsigned")) comparator_2 (.a(Op), .b(4'b1110), .lt(comparator_2_lt));  // open: gt, eq
  Comparator #(.width(4), .mode("unsigned")) comparator_3 (.a(Op), .b(4'b0011), .eq(comparator_3_eq));  // open: gt, lt
  Comparator #(.width(4), .mode("unsigned")) comparator_4 (
    .a(_4_7), .b(4'b0111), .gt(comparator_4_gt));  // open: eq, lt
  or or_1 (or_1_out, comparator_5_gt, comparator_5_eq);
  Comparator #(.width(4), .mode("unsigned")) comparator_5 (
    .a(_4_7), .b(4'b0000), .gt(comparator_5_gt), .eq(comparator_5_eq));  // open: lt
  Comparator #(.width(4), .mode("unsigned")) comparator_6 (
    .a(_4_7), .b(4'b0110), .lt(comparator_6_lt));  // open: gt, eq
  Comparator #(.width(4), .mode("unsigned")) comparator_7 (.a(Op), .b(4'b0011), .eq(comparator_7_eq));  // open: gt, lt
  Multiplexer multiplexer_2 (
    .in0(multiplexer_1_out), .in1(RSTRF_F0_out), .out(multiplexer_2_out), .sel(RSTRF));  // open: en
  and and_1 (and_1_out, comparator_1_gt, comparator_2_lt);
  and and_2 (and_2_out, comparator_3_eq, comparator_4_gt);
  and and_3 (and_3_out, or_1_out, comparator_6_lt);
  Comparator #(.width(4), .mode("unsigned")) comparator_8 (
    .a(_4_7), .b(4'b0110), .eq(comparator_8_eq));  // open: gt, lt
  Comparator #(.width(4), .mode("unsigned")) comparator_9 (
    .a(_4_7), .b(4'b0111), .eq(comparator_9_eq));  // open: gt, lt
  and and_4 (and_4_out, comparator_9_eq, comparator_10_eq);
  Comparator #(.width(4), .mode("unsigned")) comparator_10 (
    .a(_0_3), .b(4'b1000), .eq(comparator_10_eq));  // open: gt, lt
  BitSelector #(.width(16)) bitselector_1 (.in(R_d), .out(bitselector_1_out), .sel(4'b1111));
  and and_5 (and_5_out, comparator_3_eq, and_3_out);
  and and_6 (and_6_out, comparator_7_eq, comparator_8_eq);
  and and_7 (RSTRF, comparator_7_eq, and_4_out);
  Multiplexer multiplexer_3 (
    .in0(multiplexer_2_out), .in1(bitselector_1_out), .out(multiplexer_3_out), .sel(ARITH_LOGICAL_SHIFT));  // open: en
  or or_2 (ARITH_LOGICAL_SHIFT, and_1_out, and_2_out, and_5_out);
  or or_3 (FLAG, and_6_out, RSTRF);
  or or_4 (or_4_out, ARITH_LOGICAL_SHIFT, FLAG);
  Multiplexer multiplexer_4 (.in0(F0), .in1(multiplexer_3_out), .out(multiplexer_4_out), .sel(or_4_out));  // open: en
  Comparator #(.width(4), .mode("unsigned")) comparator_11 (
    .a(Op), .b(4'b0011), .gt(comparator_11_gt));  // open: eq, lt
  Comparator #(.width(4), .mode("unsigned")) comparator_12 (
    .a(Op), .b(4'b0110), .lt(comparator_12_lt));  // open: gt, eq
  BitSelector #(.width(16)) bitselector_2 (.in(RAM_out), .out(bitselector_2_out), .sel(4'b1111));
  and and_8 (load, comparator_11_gt, comparator_12_lt);
  Multiplexer multiplexer_5 (.in0(multiplexer_4_out), .in1(bitselector_2_out), .out(F0_out), .sel(load));  // open: en

  // Notes on the sheet:
  //   If ARITH/LOGIC
  //   If INC/DEC
  //   If SHIFT
  //   If FSET/ON/OFF
  //   IF RSTRF
endmodule

module update_F1 (
  input  FON_F1_out,
  input  FSET5_F1_out,
  input  FOFF_F1_out,
  input  FSET4_F1_out,
  input  RSTRF_F1_out,
  input  [2:0] _9_11,
  input  [3:0] _4_7,
  input  [3:0] _0_3,
  input  [15:0] R_d,
  input  F1,
  input  [3:0] Op,
  input  [15:0] RAM_out,
  output F1_out
);

  wire and_1_out, and_2_out, and_3_out, and_4_out, and_6_out, and_7_out, ARITH_LOGICAL_SHIFT,
       comparator_1_eq, comparator_1_gt, comparator_2_lt, comparator_3_eq, comparator_4_gt, comparator_5_lt,
       comparator_6_eq, comparator_7_gt, comparator_8_eq, comparator_9_eq, comparator_10_eq,
       comparator_11_eq, comparator_12_eq, comparator_13_gt, comparator_14_lt, FLAG, load, multiplexer_1_out,
       multiplexer_2_out, multiplexer_3_out, multiplexer_4_out, or_1_out, or_4_out, RSTRF;

  Multiplexer #(.select(3)) multiplexer_1 (
    .in0(FON_F1_out), .in2(FSET5_F1_out), .in4(FOFF_F1_out), .in6(FSET4_F1_out), .out(multiplexer_1_out),
    .sel(_9_11));  // open: in1, in3, in5, in7, en
  Comparator #(.width(4), .mode("unsigned")) comparator_1 (
    .a(_4_7), .b(4'b0000), .gt(comparator_1_gt), .eq(comparator_1_eq));  // open: lt
  Comparator #(.width(4), .mode("unsigned")) comparator_2 (
    .a(_4_7), .b(4'b0110), .lt(comparator_2_lt));  // open: gt, eq
  Comparator #(.width(4), .mode("unsigned")) comparator_3 (.a(Op), .b(4'b0011), .eq(comparator_3_eq));  // open: gt, lt
  Multiplexer multiplexer_2 (
    .in0(multiplexer_1_out), .in1(RSTRF_F1_out), .out(multiplexer_2_out), .sel(RSTRF));  // open: en
  Comparator #(.width(4), .mode("unsigned")) comparator_4 (.a(Op), .b(4'b0111), .gt(comparator_4_gt));  // open: eq, lt
  and and_1 (and_1_out, comparator_4_gt, comparator_5_lt);
  Comparator #(.width(4), .mode("unsigned")) comparator_5 (.a(Op), .b(4'b1110), .lt(comparator_5_lt));  // open: gt, eq
  Comparator #(.width(4), .mode("unsigned")) comparator_6 (.a(Op), .b(4'b0011), .eq(comparator_6_eq));  // open: gt, lt
  Comparator #(.width(4), .mode("unsigned")) comparator_7 (
    .a(_4_7), .b(4'b0111), .gt(comparator_7_gt));  // open: eq, lt
  or or_1 (or_1_out, comparator_1_gt, comparator_1_eq);
  and and_2 (and_2_out, or_1_out, comparator_2_lt);
  Comparator #(.width(4), .mode("unsigned")) comparator_8 (
    .a(_4_7), .b(4'b0110), .eq(comparator_8_eq));  // open: gt, lt
  Comparator #(.width(4), .mode("unsigned")) comparator_9 (
    .a(_4_7), .b(4'b0111), .eq(comparator_9_eq));  // open: gt, lt
  Comparator #(.width(4), .mode("unsigned")) comparator_10 (
    .a(_0_3), .b(4'b1000), .eq(comparator_10_eq));  // open: gt, lt
  Comparator #(.width(16)) comparator_11 (.a(R_d), .b({16{1'b0}}), .eq(comparator_11_eq));  // open: gt, lt
  and and_3 (and_3_out, comparator_6_eq, comparator_7_gt);
  and and_4 (and_4_out, comparator_6_eq, and_2_out);
  and and_5 (RSTRF, comparator_3_eq, and_6_out);
  and and_6 (and_6_out, comparator_9_eq, comparator_10_eq);
  Multiplexer multiplexer_3 (
    .in0(multiplexer_2_out), .in1(comparator_11_eq), .out(multiplexer_3_out), .sel(ARITH_LOGICAL_SHIFT));  // open: en
  or or_2 (ARITH_LOGICAL_SHIFT, and_1_out, and_3_out, and_4_out);
  and and_7 (and_7_out, comparator_3_eq, comparator_8_eq);
  or or_3 (FLAG, and_7_out, RSTRF);
  or or_4 (or_4_out, ARITH_LOGICAL_SHIFT, FLAG);
  Multiplexer multiplexer_4 (.in0(F1), .in1(multiplexer_3_out), .out(multiplexer_4_out), .sel(or_4_out));  // open: en
  Comparator #(.width(16)) comparator_12 (.a(RAM_out), .b({16{1'b0}}), .eq(comparator_12_eq));  // open: gt, lt
  Comparator #(.width(4), .mode("unsigned")) comparator_13 (
    .a(Op), .b(4'b0011), .gt(comparator_13_gt));  // open: eq, lt
  Comparator #(.width(4), .mode("unsigned")) comparator_14 (
    .a(Op), .b(4'b0110), .lt(comparator_14_lt));  // open: gt, eq
  Multiplexer multiplexer_5 (.in0(multiplexer_4_out), .in1(comparator_12_eq), .out(F1_out), .sel(load));  // open: en
  and and_8 (load, comparator_13_gt, comparator_14_lt);

  // Notes on the sheet:
  //   If ARITH/LOGIC
  //   If INC/DEC
  //   If SHIFT
  //   If FSET/ON/OFF
  //   IF RSTRF
endmodule

module update_F2 (
  input  FON_F2_out,
  input  FSET5_F2_out,
  input  FOFF_F2_out,
  input  FSET4_F2_out,
  input  RSTRF_F2_out,
  input  [2:0] _9_11,
  input  [3:0] _4_7,
  input  [3:0] _0_3,
  input  F2,
  input  [3:0] Op,
  input  ALSU_overflow,
  output F2_out
);

  wire and_2_out, and_3_out, and_5_out, and_6_out, ARITH, ARITH_SHIFT, ASL, comparator_1_eq, comparator_2_eq,
       comparator_3_gt, comparator_4_lt, comparator_5_eq, comparator_6_gt, comparator_7_eq, comparator_8_eq,
       comparator_9_eq, comparator_10_eq, FLAG, multiplexer_1_out, multiplexer_2_out, multiplexer_3_out,
       or_3_out, RSTRF;

  Comparator #(.width(4), .mode("unsigned")) comparator_1 (.a(Op), .b(4'b0011), .eq(comparator_1_eq));  // open: gt, lt
  Comparator #(.width(4), .mode("unsigned")) comparator_2 (
    .a(_4_7), .b(4'b0100), .eq(comparator_2_eq));  // open: gt, lt
  Multiplexer #(.select(3)) multiplexer_1 (
    .in0(FON_F2_out), .in2(FSET5_F2_out), .in4(FOFF_F2_out), .in6(FSET4_F2_out), .out(multiplexer_1_out),
    .sel(_9_11));  // open: in1, in3, in5, in7, en
  Comparator #(.width(4), .mode("unsigned")) comparator_3 (.a(Op), .b(4'b1001), .gt(comparator_3_gt));  // open: eq, lt
  Comparator #(.width(4), .mode("unsigned")) comparator_4 (.a(Op), .b(4'b1101), .lt(comparator_4_lt));  // open: gt, eq
  Comparator #(.width(4), .mode("unsigned")) comparator_5 (.a(Op), .b(4'b0011), .eq(comparator_5_eq));  // open: gt, lt
  Comparator #(.width(4), .mode("unsigned")) comparator_6 (
    .a(_4_7), .b(4'b0111), .gt(comparator_6_gt));  // open: eq, lt
  Comparator #(.width(4), .mode("unsigned")) comparator_7 (.a(Op), .b(4'b0011), .eq(comparator_7_eq));  // open: gt, lt
  Comparator #(.width(4), .mode("unsigned")) comparator_8 (
    .a(_4_7), .b(4'b0110), .eq(comparator_8_eq));  // open: gt, lt
  Comparator #(.width(4), .mode("unsigned")) comparator_9 (
    .a(_4_7), .b(4'b0111), .eq(comparator_9_eq));  // open: gt, lt
  Comparator #(.width(4), .mode("unsigned")) comparator_10 (
    .a(_0_3), .b(4'b1000), .eq(comparator_10_eq));  // open: gt, lt
  and and_1 (ASL, comparator_1_eq, comparator_2_eq);
  Multiplexer multiplexer_2 (
    .in0(multiplexer_1_out), .in1(RSTRF_F2_out), .out(multiplexer_2_out), .sel(RSTRF));  // open: en
  and and_2 (and_2_out, comparator_3_gt, comparator_4_lt);
  and and_3 (and_3_out, comparator_5_eq, comparator_6_gt);
  and and_4 (RSTRF, comparator_7_eq, and_5_out);
  and and_5 (and_5_out, comparator_9_eq, comparator_10_eq);
  or or_1 (ARITH, and_2_out, and_3_out);
  and and_6 (and_6_out, comparator_7_eq, comparator_8_eq);
  Multiplexer multiplexer_3 (
    .in0(multiplexer_2_out), .in1(ALSU_overflow), .out(multiplexer_3_out), .sel(ARITH_SHIFT));  // open: en
  or or_2 (FLAG, and_6_out, RSTRF);
  or or_3 (or_3_out, ARITH_SHIFT, FLAG);
  or or_4 (ARITH_SHIFT, ARITH, ASL);
  Multiplexer multiplexer_4 (.in0(F2), .in1(multiplexer_3_out), .out(F2_out), .sel(or_3_out));  // open: en

  // Notes on the sheet:
  //   If FSET/ON/OFF
  //   IF RSTRF
  //   If ADD/SUB/MUL
  //   If INC/DEC
endmodule

module update_F3 (
  input  FON_F3_out,
  input  FSET5_F3_out,
  input  FOFF_F3_out,
  input  FSET4_F3_out,
  input  RSTRF_F3_out,
  input  [2:0] _9_11,
  input  [3:0] _4_7,
  input  [3:0] _0_3,
  input  F3,
  input  [3:0] Op,
  input  ALSU_carry_out,
  output F3_out
);

  wire and_1_out, and_2_out, and_3_out, and_4_out, and_5_out, ARITH_SHIFT, comparator_1_eq, comparator_2_eq,
       comparator_3_eq, comparator_4_eq, comparator_5_eq, comparator_6_eq, comparator_7_eq, comparator_8_eq,
       comparator_9_gt, comparator_10_lt, comparator_11_eq, comparator_12_gt, FLAG, multiplexer_1_out,
       multiplexer_2_out, multiplexer_3_out, or_1_out, or_3_out, RSTRF;

  Multiplexer #(.select(3)) multiplexer_1 (
    .in0(FON_F3_out), .in2(FSET5_F3_out), .in4(FOFF_F3_out), .in6(FSET4_F3_out), .out(multiplexer_1_out),
    .sel(_9_11));  // open: in1, in3, in5, in7, en
  Comparator #(.width(4), .mode("unsigned")) comparator_1 (
    .a(_4_7), .b(4'b0000), .eq(comparator_1_eq));  // open: gt, lt
  Comparator #(.width(4), .mode("unsigned")) comparator_2 (
    .a(_4_7), .b(4'b0001), .eq(comparator_2_eq));  // open: gt, lt
  Comparator #(.width(4), .mode("unsigned")) comparator_3 (
    .a(_4_7), .b(4'b0100), .eq(comparator_3_eq));  // open: gt, lt
  Comparator #(.width(4), .mode("unsigned")) comparator_4 (
    .a(_4_7), .b(4'b0101), .eq(comparator_4_eq));  // open: gt, lt
  Comparator #(.width(4), .mode("unsigned")) comparator_5 (.a(Op), .b(4'b0011), .eq(comparator_5_eq));  // open: gt, lt
  Comparator #(.width(4), .mode("unsigned")) comparator_6 (
    .a(_4_7), .b(4'b0110), .eq(comparator_6_eq));  // open: gt, lt
  Comparator #(.width(4), .mode("unsigned")) comparator_7 (
    .a(_4_7), .b(4'b0111), .eq(comparator_7_eq));  // open: gt, lt
  Comparator #(.width(4), .mode("unsigned")) comparator_8 (
    .a(_0_3), .b(4'b1000), .eq(comparator_8_eq));  // open: gt, lt
  Multiplexer multiplexer_2 (
    .in0(multiplexer_1_out), .in1(RSTRF_F3_out), .out(multiplexer_2_out), .sel(RSTRF));  // open: en
  Comparator #(.width(4), .mode("unsigned")) comparator_9 (.a(Op), .b(4'b1001), .gt(comparator_9_gt));  // open: eq, lt
  and and_1 (and_1_out, comparator_9_gt, comparator_10_lt);
  Comparator #(.width(4), .mode("unsigned")) comparator_10 (
    .a(Op), .b(4'b1101), .lt(comparator_10_lt));  // open: gt, eq
  Comparator #(.width(4), .mode("unsigned")) comparator_11 (
    .a(Op), .b(4'b0011), .eq(comparator_11_eq));  // open: gt, lt
  Comparator #(.width(4), .mode("unsigned")) comparator_12 (
    .a(_4_7), .b(4'b0111), .gt(comparator_12_gt));  // open: eq, lt
  or or_1 (or_1_out, comparator_1_eq, comparator_2_eq, comparator_3_eq, comparator_4_eq);
  and and_2 (and_2_out, comparator_7_eq, comparator_8_eq);
  and and_3 (and_3_out, comparator_11_eq, comparator_12_gt);
  and and_4 (and_4_out, comparator_11_eq, or_1_out);
  and and_5 (and_5_out, comparator_5_eq, comparator_6_eq);
  and and_6 (RSTRF, comparator_5_eq, and_2_out);
  Multiplexer multiplexer_3 (
    .in0(multiplexer_2_out), .in1(ALSU_carry_out), .out(multiplexer_3_out), .sel(ARITH_SHIFT));  // open: en
  or or_2 (FLAG, and_5_out, RSTRF);
  or or_3 (or_3_out, ARITH_SHIFT, FLAG);
  or or_4 (ARITH_SHIFT, and_1_out, and_3_out, and_4_out);
  Multiplexer multiplexer_4 (.in0(F3), .in1(multiplexer_3_out), .out(F3_out), .sel(or_3_out));  // open: en

  // Notes on the sheet:
  //   IF RSTRF
  //   If INC/DEC
  //   If SHIFT that has carry
  //   LSL,LSR,ASL,ASR
  //   If FSET/ON/OFF
  //   If ARITH
endmodule

module update_F4 (
  input  FON_F4_out,
  input  FSET5_F4_out,
  input  FOFF_F4_out,
  input  FSET4_F4_out,
  input  RSTRF_F4_out,
  input  [2:0] _9_11,
  input  [3:0] _4_7,
  input  [3:0] _0_3,
  input  F4,
  input  [3:0] Op,
  input  [15:0] Op_code,
  output F4_out
);

  wire and_1_out, and_2_out, CBON, comparator_1_eq, comparator_2_eq, comparator_3_eq, comparator_4_eq, FLAG,
       multiplexer_1_out, multiplexer_2_out, multiplexer_3_out, or_1_out, RSTRF;

  Multiplexer #(.select(3)) multiplexer_1 (
    .in0(FON_F4_out), .in2(FSET5_F4_out), .in4(FOFF_F4_out), .in6(FSET4_F4_out), .out(multiplexer_1_out),
    .sel(_9_11));  // open: in1, in3, in5, in7, en
  Multiplexer multiplexer_2 (
    .in0(multiplexer_1_out), .in1(RSTRF_F4_out), .out(multiplexer_2_out), .sel(RSTRF));  // open: en
  Comparator #(.width(4), .mode("unsigned")) comparator_1 (.a(Op), .b(4'b0011), .eq(comparator_1_eq));  // open: gt, lt
  Multiplexer multiplexer_3 (.in0(multiplexer_2_out), .in1(1'b1), .out(multiplexer_3_out), .sel(CBON));  // open: en
  Comparator #(.width(4), .mode("unsigned")) comparator_2 (
    .a(_4_7), .b(4'b0110), .eq(comparator_2_eq));  // open: gt, lt
  Comparator #(.width(4), .mode("unsigned")) comparator_3 (
    .a(_4_7), .b(4'b0111), .eq(comparator_3_eq));  // open: gt, lt
  and and_1 (and_1_out, comparator_3_eq, comparator_4_eq);
  Comparator #(.width(4), .mode("unsigned")) comparator_4 (
    .a(_0_3), .b(4'b1000), .eq(comparator_4_eq));  // open: gt, lt
  or or_1 (or_1_out, CBON, FLAG);
  and and_2 (and_2_out, comparator_1_eq, comparator_2_eq);
  and and_3 (RSTRF, comparator_1_eq, and_1_out);
  Comparator #(.width(16)) comparator_5 (.a(Op_code), .b(16'h3160), .eq(CBON));  // open: gt, lt
  Multiplexer multiplexer_4 (.in0(F4), .in1(multiplexer_3_out), .out(F4_out), .sel(or_1_out));  // open: en
  or or_2 (FLAG, and_2_out, RSTRF);

  // Notes on the sheet:
  //   If FSET/ON/OFF
  //   IF RSTRF
endmodule

module update_flags (
  input  [15:0] Op_code,
  input  [15:0] R_d,
  input  [15:0] R_data_out,
  input  ALSU_overflow,
  input  ALSU_carry_out,
  input  F0,
  input  F1,
  input  F2,
  input  F3,
  input  F4,
  input  [15:0] RAM_out,
  output F0_out,
  output F1_out,
  output F2_out,
  output F3_out,
  output F4_out
);

  wire _6_6, _7_7, FOFF_F0_out, FOFF_F1_out, FOFF_F2_out, FOFF_F3_out, FOFF_F4_out, FON_F0_out, FON_F1_out,
       FON_F2_out, FON_F3_out, FON_F4_out, FSET4_F0_out, FSET4_F1_out, FSET4_F2_out, FSET4_F3_out,
       FSET5_F0_out, FSET5_F1_out, FSET5_F2_out, FSET5_F3_out, FSET5_F4_out, RSTRF_F0_out, RSTRF_F1_out,
       RSTRF_F2_out, RSTRF_F3_out, RSTRF_F4_out;
  wire [2:0] _4_6, _9_11;
  wire [3:0] shifter_1_out;
  wire [5:0] _0_5;
  wire [7:0] _0_7;

  BitSelector #(.width(16), .group(8)) bitselector_1 (.in(Op_code), .out(_0_7), .sel(1'b0));
  BitSelector #(.width(16), .group(6)) bitselector_2 (.in(Op_code), .out(_0_5), .sel(2'b00));
  BitSelector #(.width(16)) bitselector_3 (.in(Op_code), .out(_6_6), .sel(4'b0110));
  BitSelector #(.width(16)) bitselector_4 (.in(Op_code), .out(_7_7), .sel(4'b0111));
  BitSelector #(.width(4), .group(3)) bitselector_5 (.in(Op_code[7:4]), .out(_4_6), .sel(1'b0));
  BitSelector #(.width(4), .group(3)) bitselector_6 (.in(shifter_1_out), .out(_9_11), .sel(1'b0));
  Shifter #(.width(4), .shift("lr")) shifter_1 (.in(Op_code[11:8]), .\dist (2'b01), .out(shifter_1_out));
  FON FON (
    .F0(F0), .F1(F1), .F2(F2), .F3(F3), .F4(F4), .Op_code(Op_code), .F0_out(FON_F0_out), .F1_out(FON_F1_out),
    .F2_out(FON_F2_out), .F3_out(FON_F3_out), .F4_out(FON_F4_out));
  FOFF FOFF (
    .F0(F0), .F1(F1), .F2(F2), .F3(F3), .F4(F4), .Op_code(Op_code), .F0_out(FOFF_F0_out),
    .F1_out(FOFF_F1_out), .F2_out(FOFF_F2_out), .F3_out(FOFF_F3_out), .F4_out(FOFF_F4_out));
  update_F0 update_F0 (
    .FON_F0_out(FON_F0_out), .FSET5_F0_out(FSET5_F0_out), .FOFF_F0_out(FOFF_F0_out),
    .FSET4_F0_out(FSET4_F0_out), .RSTRF_F0_out(RSTRF_F0_out), ._9_11(_9_11), ._4_7(Op_code[7:4]),
    ._0_3(Op_code[3:0]), .R_d(R_data_out), .F0(F0), .Op(Op_code[15:12]), .RAM_out(RAM_out), .F0_out(F0_out));
  update_F1 update_F1 (
    .FON_F1_out(FON_F1_out), .FSET5_F1_out(FSET5_F1_out), .FOFF_F1_out(FOFF_F1_out),
    .FSET4_F1_out(FSET4_F1_out), .RSTRF_F1_out(RSTRF_F1_out), ._9_11(_9_11), ._4_7(Op_code[7:4]),
    ._0_3(Op_code[3:0]), .R_d(R_data_out), .F1(F1), .Op(Op_code[15:12]), .RAM_out(RAM_out), .F1_out(F1_out));
  update_F4 update_F4 (
    .FON_F4_out(FON_F4_out), .FSET5_F4_out(FSET5_F4_out), .FOFF_F4_out(FOFF_F4_out), .FSET4_F4_out(F4),
    .RSTRF_F4_out(RSTRF_F4_out), ._9_11(_9_11), ._4_7(Op_code[7:4]), ._0_3(Op_code[3:0]), .F4(F4),
    .Op(Op_code[15:12]), .Op_code(Op_code), .F4_out(F4_out));
  RSTRF RSTRF (
    .R_d(R_d), .F0(RSTRF_F0_out), .F1(RSTRF_F1_out), .F2(RSTRF_F2_out), .F3(RSTRF_F3_out), .F4(RSTRF_F4_out));
  FSET5 FSET5 (
    .Op_code(Op_code), .F0_out(FSET5_F0_out), .F1_out(FSET5_F1_out), .F2_out(FSET5_F2_out),
    .F3_out(FSET5_F3_out), .F4_out(FSET5_F4_out));
  FSET4 FSET4 (
    .Op_code(Op_code), .F0_out(FSET4_F0_out), .F1_out(FSET4_F1_out), .F2_out(FSET4_F2_out),
    .F3_out(FSET4_F3_out));
  update_F2 update_F2 (
    .FON_F2_out(FON_F2_out), .FSET5_F2_out(FSET5_F2_out), .FOFF_F2_out(FOFF_F2_out),
    .FSET4_F2_out(FSET4_F2_out), .RSTRF_F2_out(RSTRF_F2_out), ._9_11(_9_11), ._4_7(Op_code[7:4]),
    ._0_3(Op_code[3:0]), .F2(F2), .Op(Op_code[15:12]), .ALSU_overflow(ALSU_overflow), .F2_out(F2_out));
  update_F3 update_F3 (
    .FON_F3_out(FON_F3_out), .FSET5_F3_out(FSET5_F3_out), .FOFF_F3_out(FOFF_F3_out),
    .FSET4_F3_out(FSET4_F3_out), .RSTRF_F3_out(RSTRF_F3_out), ._9_11(_9_11), ._4_7(Op_code[7:4]),
    ._0_3(Op_code[3:0]), .F3(F3), .Op(Op_code[15:12]), .ALSU_carry_out(ALSU_carry_out), .F3_out(F3_out));

  // Other names for the same wires on the sheet: FSET4_F4_out = F4; _0_3[3:0] = Op_code[3:0];
  //   _4_7[3:0] = Op_code[7:4]; _8_11[3:0] = Op_code[11:8]; Op[3:0] = Op_code[15:12]
endmodule

module RAM (
  input  [15:0] Op_code,
  input  [15:0] R_b,
  output [15:0] RAM_address,
  output load,
  output load_store
);

  wire bitselector_2_out, comparator_1_gt, comparator_2_lt;
  wire [4:4] offset;
  wire [15:0] bit_extender_1_out;

  BitSelector #(.width(4)) bitselector_1 (.in(Op_code[15:12]), .out(offset[4]), .sel(2'b00));
  assign bit_extender_1_out = {{11{1'b0}}, {offset[4], Op_code[7:4]}};  // Bit_Extender bit_extender_1
  Comparator #(.width(4), .mode("unsigned")) comparator_1 (
    .a(Op_code[15:12]), .b(4'b0011), .gt(comparator_1_gt));  // open: eq, lt
  Comparator #(.width(4), .mode("unsigned")) comparator_2 (
    .a(Op_code[15:12]), .b(4'b1000), .lt(comparator_2_lt));  // open: gt, eq
  Adder #(.width(16)) adder_1 (.a(bit_extender_1_out), .b(R_b), .out(RAM_address));  // open: cin, cout
  BitSelector #(.width(4)) bitselector_2 (.in(Op_code[15:12]), .out(bitselector_2_out), .sel(2'b01));
  and and_1 (load_store, comparator_1_gt, comparator_2_lt);
  not not_1 (load, bitselector_2_out);

  // Other names for the same wires on the sheet: _4_7[3:0] = Op_code[7:4]; offset[3:0] = Op_code[7:4];
  //   _0_3[3:0] = Op_code[3:0]; _8_11[3:0] = Op_code[11:8]; Op[3:0] = Op_code[15:12]
endmodule

module BRANCH (
  input  [15:0] Op_code,
  input  [15:0] PC_in,
  input  [15:0] R_b,
  input  [15:0] R13,
  input  CALL_RETURN,
  input  F0,
  input  F1,
  input  F2,
  input  F3,
  input  called_interrupt_handler_yet,
  input  interrupted_this_cycle,
  output [15:0] PC_out,
  output branch
);

  wire absolute, and_1_out, branch_t, comparator_1_eq, comparator_2_eq, comparator_3_eq, comparator_4_eq,
       interrupted_and_haven_t_called_handler_yet, not_1_out, or_2_out;
  wire [15:0] multiplexer_1_out, multiplexer_2_out, PC_absolute, PC_relative;

  Comparator #(.width(4)) comparator_1 (.a(Op_code[15:12]), .b(4'b0001), .eq(comparator_1_eq));  // open: gt, lt
  Comparator #(.width(4)) comparator_2 (.a(Op_code[11:8]), .b(4'b0001), .eq(comparator_2_eq));  // open: gt, lt
  Comparator #(.width(4)) comparator_3 (.a(Op_code[7:4]), .b(4'b0000), .eq(comparator_3_eq));  // open: gt, lt
  Comparator #(.width(4)) comparator_4 (.a(Op_code[15:12]), .b(4'b0000), .eq(comparator_4_eq));  // open: gt, lt
  not not_1 (not_1_out, comparator_2_eq);
  and and_1 (and_1_out, comparator_1_eq, not_1_out, comparator_3_eq);
  RELATIVE relative_1 (.Op_code(Op_code), .PC_in(PC_in), .F0(F0), .F1(F1), .F2(F2), .F3(F3), .PC_relative(PC_relative));
  ABSOLUTE absolute_1 (
    .Op_code(Op_code), .PC_in(PC_in), .R_b(R_b), .F0(F0), .F1(F1), .F2(F2), .F3(F3), .PC_absolute(PC_absolute));
  or or_1 (branch_t, comparator_4_eq, and_1_out);
  Multiplexer #(.width(16)) multiplexer_1 (
    .in0(PC_relative), .in1(PC_absolute), .out(multiplexer_1_out), .sel(absolute));  // open: en
  BitSelector #(.width(4)) bitselector_1 (.in(Op_code[15:12]), .out(absolute), .sel(2'b00));
  Multiplexer #(.width(16)) multiplexer_2 (
    .in0(multiplexer_1_out), .in1(PC_in), .out(multiplexer_2_out),
    .sel(interrupted_and_haven_t_called_handler_yet));  // open: en
  Multiplexer multiplexer_3 (.in0(branch_t), .in1(1'b1), .out(branch), .sel(or_2_out));  // open: en
  or or_2 (or_2_out, CALL_RETURN, interrupted_and_haven_t_called_handler_yet);
  and and_2 (interrupted_and_haven_t_called_handler_yet, ~called_interrupt_handler_yet, interrupted_this_cycle);  // AND_Gate
  Multiplexer #(.width(16)) multiplexer_4 (
    .in0(multiplexer_2_out), .in1(R13), .out(PC_out), .sel(CALL_RETURN));  // open: en

  // Other names for the same wires on the sheet: interrupted_thiis_cycle = interrupted_this_cycle;
  //   _0_3[3:0] = Op_code[3:0]; _4_7[3:0] = Op_code[7:4]; _8_11[3:0] = Op_code[11:8]; Op[3:0] = Op_code[15:12]
endmodule

module RELATIVE (
  input  [15:0] Op_code,
  input  [15:0] PC_in,
  input  F0,
  input  F1,
  input  F2,
  input  F3,
  output [15:0] PC_relative
);

  wire nor_1_out, nor_2_out, not_1_out, not_2_out, not_3_out, not_4_out, or_1_out, or_2_out, xnor_1_out,
       xor_1_out, xor_2_out, xor_3_out;
  wire [15:0] BCR, BGER, BGR, BLER, BLR, BNCR, BNSR, BNVR, BNZR, BRR, BSR, BUGR, BULER, BVR, BZR, offset,
       PC_no_branch;

  Multiplexer #(.width(16)) multiplexer_1 (.in0(PC_no_branch), .in1(BRR), .out(BLR), .sel(xor_1_out));  // open: en
  xor xor_1 (xor_1_out, F0, F2);
  Multiplexer #(.width(16)) multiplexer_2 (.in0(PC_no_branch), .in1(BRR), .out(BGER), .sel(xnor_1_out));  // open: en
  xnor xnor_1 (xnor_1_out, F0, F2);
  Multiplexer #(.width(16)) multiplexer_3 (.in0(PC_no_branch), .in1(BRR), .out(BLER), .sel(or_1_out));  // open: en
  or or_1 (or_1_out, xor_2_out, F1);
  Multiplexer #(.width(16)) multiplexer_4 (.in0(PC_no_branch), .in1(BRR), .out(BGR), .sel(nor_1_out));  // open: en
  nor nor_1 (nor_1_out, xor_3_out, F1);
  Multiplexer #(.width(16)) multiplexer_5 (.in0(PC_no_branch), .in1(BRR), .out(BULER), .sel(or_2_out));  // open: en
  or or_2 (or_2_out, ~F3, F1);  // OR_Gate
  Multiplexer #(.width(16)) multiplexer_6 (.in0(PC_no_branch), .in1(BRR), .out(BUGR), .sel(nor_2_out));  // open: en
  nor nor_2 (nor_2_out, ~F3, F1);  // NOR_Gate
  Adder #(.width(16)) adder_1 (.a(PC_in), .b(offset), .out(BRR));  // open: cin, cout
  Adder #(.width(16)) adder_2 (.a(PC_in), .b(16'h1), .out(PC_no_branch));  // open: cin, cout
  xor xor_2 (xor_2_out, F0, F2);
  xor xor_3 (xor_3_out, F0, F2);
  assign offset = {{8{Op_code[7]}}, Op_code[7:0]};  // Bit_Extender bit_extender_1
  Multiplexer #(.width(16)) multiplexer_7 (.in0(PC_no_branch), .in1(BRR), .out(BZR), .sel(F1));  // open: en
  Multiplexer #(.width(16)) multiplexer_8 (.in0(PC_no_branch), .in1(BRR), .out(BNZR), .sel(not_1_out));  // open: en
  not not_1 (not_1_out, F1);
  Multiplexer #(.width(16)) multiplexer_9 (.in0(PC_no_branch), .in1(BRR), .out(BCR), .sel(F3));  // open: en
  Multiplexer #(.width(16)) multiplexer_10 (.in0(PC_no_branch), .in1(BRR), .out(BNCR), .sel(not_2_out));  // open: en
  not not_2 (not_2_out, F3);
  Multiplexer #(.width(16)) multiplexer_11 (.in0(PC_no_branch), .in1(BRR), .out(BSR), .sel(F0));  // open: en
  Multiplexer #(.width(16)) multiplexer_12 (.in0(PC_no_branch), .in1(BRR), .out(BNSR), .sel(not_3_out));  // open: en
  not not_3 (not_3_out, F0);
  Multiplexer #(.width(16)) multiplexer_13 (.in0(PC_no_branch), .in1(BRR), .out(BVR), .sel(F2));  // open: en
  Multiplexer #(.width(16)) multiplexer_14 (.in0(PC_no_branch), .in1(BRR), .out(BNVR), .sel(not_4_out));  // open: en
  not not_4 (not_4_out, F2);
  Multiplexer #(.select(4), .width(16)) multiplexer_15 (
    .in0(BRR), .in2(BLR), .in3(BGER), .in4(BLER), .in5(BGR), .in6(BULER), .in7(BUGR), .in8(BZR), .in9(BNZR),
    .in10(BCR), .in11(BNCR), .in12(BSR), .in13(BNSR), .in14(BVR), .in15(BNVR), .out(PC_relative),
    .sel(Op_code[11:8]));  // open: in1, en

  // Other names for the same wires on the sheet: _0_7[7:0] = Op_code[7:0]; _8_11[3:0] = Op_code[11:8];
  //   Op[3:0] = Op_code[15:12]; PC_branch[15:0] = BRR
endmodule

module ABSOLUTE (
  input  [15:0] Op_code,
  input  [15:0] PC_in,
  input  [15:0] R_b,
  input  F0,
  input  F1,
  input  F2,
  input  F3,
  output [15:0] PC_absolute
);

  wire nor_1_out, nor_2_out, not_1_out, not_2_out, not_3_out, not_4_out, or_1_out, or_2_out, xnor_1_out,
       xor_1_out, xor_2_out, xor_3_out;
  wire [15:0] BC, BG, BGE, BL, BLE, BNC, BNS, BNV, BNZ, BS, BUG, BULE, BV, BZ, PC_no_branch;

  Multiplexer #(.width(16)) multiplexer_1 (.in0(PC_no_branch), .in1(R_b), .out(BL), .sel(xor_1_out));  // open: en
  xor xor_1 (xor_1_out, F0, F2);
  Multiplexer #(.width(16)) multiplexer_2 (.in0(PC_no_branch), .in1(R_b), .out(BGE), .sel(xnor_1_out));  // open: en
  xnor xnor_1 (xnor_1_out, F0, F2);
  Multiplexer #(.width(16)) multiplexer_3 (.in0(PC_no_branch), .in1(R_b), .out(BLE), .sel(or_1_out));  // open: en
  or or_1 (or_1_out, xor_2_out, F1);
  Multiplexer #(.width(16)) multiplexer_4 (.in0(PC_no_branch), .in1(R_b), .out(BG), .sel(nor_1_out));  // open: en
  nor nor_1 (nor_1_out, xor_3_out, F1);
  Multiplexer #(.width(16)) multiplexer_5 (.in0(PC_no_branch), .in1(R_b), .out(BULE), .sel(or_2_out));  // open: en
  or or_2 (or_2_out, ~F3, F1);  // OR_Gate
  Multiplexer #(.width(16)) multiplexer_6 (.in0(PC_no_branch), .in1(R_b), .out(BUG), .sel(nor_2_out));  // open: en
  nor nor_2 (nor_2_out, ~F3, F1);  // NOR_Gate
  Adder #(.width(16)) adder_1 (.a(PC_in), .b(16'h1), .out(PC_no_branch));  // open: cin, cout
  xor xor_2 (xor_2_out, F0, F2);
  xor xor_3 (xor_3_out, F0, F2);
  Multiplexer #(.width(16)) multiplexer_7 (.in0(PC_no_branch), .in1(R_b), .out(BZ), .sel(F1));  // open: en
  Multiplexer #(.width(16)) multiplexer_8 (.in0(PC_no_branch), .in1(R_b), .out(BNZ), .sel(not_1_out));  // open: en
  not not_1 (not_1_out, F1);
  Multiplexer #(.width(16)) multiplexer_9 (.in0(PC_no_branch), .in1(R_b), .out(BC), .sel(F3));  // open: en
  Multiplexer #(.width(16)) multiplexer_10 (.in0(PC_no_branch), .in1(R_b), .out(BNC), .sel(not_2_out));  // open: en
  not not_2 (not_2_out, F3);
  Multiplexer #(.width(16)) multiplexer_11 (.in0(PC_no_branch), .in1(R_b), .out(BS), .sel(F0));  // open: en
  Multiplexer #(.width(16)) multiplexer_12 (.in0(PC_no_branch), .in1(R_b), .out(BNS), .sel(not_3_out));  // open: en
  not not_3 (not_3_out, F0);
  Multiplexer #(.width(16)) multiplexer_13 (.in0(PC_no_branch), .in1(R_b), .out(BV), .sel(F2));  // open: en
  Multiplexer #(.width(16)) multiplexer_14 (.in0(PC_no_branch), .in1(R_b), .out(BNV), .sel(not_4_out));  // open: en
  not not_4 (not_4_out, F2);
  Multiplexer #(.select(4), .width(16)) multiplexer_15 (
    .in0(R_b), .in2(BL), .in3(BGE), .in4(BLE), .in5(BG), .in6(BULE), .in7(BUG), .in8(BZ), .in9(BNZ),
    .in10(BC), .in11(BNC), .in12(BS), .in13(BNS), .in14(BV), .in15(BNV), .out(PC_absolute),
    .sel(Op_code[11:8]));  // open: in1, en

  // Other names for the same wires on the sheet: _0_7[7:0] = Op_code[7:0]; _8_11[3:0] = Op_code[11:8];
  //   Op[3:0] = Op_code[15:12]; BR[15:0] = R_b; PC_branch[15:0] = R_b
endmodule

module interrupt_state (
  input  CLK,
  input  [15:0] Op_code,
  input  [6:0] keyboard_out,
  output called_interrupted_handler_yet,
  output resolved_interrupt_handler_yet,
  output interrupted_this_cycle,
  output [6:0] cur_char,
  output [2:0] thread_number
);

  wire and_1_out, and_2_out, and_3_out, and_4_out, and_5_out, and_6_out, and_7_out, and_8_out, and_10_out,
       comparator_1_eq, comparator_2_eq, comparator_3_eq, comparator_4_eq, cycle_number_is_multiple_of_16,
       multiplexer_2_out, multiplexer_3_out, Op_code_is_CALL, Op_code_is_RETURN, or_1_out, or_2_out,
       or_3_out, or_4_out, or_5_out, valid_char, valid_cur_char, valid_cur_char_and_not_return,
       valid_thread_number;
  wire [3:0] counter_1_q;
  wire [6:0] multiplexer_1_out;
  wire [7:0] bitselector_1_out, bitselector_2_out;

  not not_1 (valid_char, comparator_1_eq);
  Comparator #(.width(7)) comparator_1 (.a(keyboard_out), .b({7{1'b0}}), .eq(comparator_1_eq));  // open: gt, lt
  and and_1 (and_1_out, interrupted_this_cycle, Op_code_is_RETURN, resolved_interrupt_handler_yet);
  Comparator #(.width(7)) comparator_2 (.a(cur_char), .b({7{1'b0}}), .eq(comparator_2_eq));  // open: gt, lt
  Comparator #(.width(7)) comparator_3 (.a(cur_char), .b({7{1'b0}}), .eq(comparator_3_eq));  // open: gt, lt
  Multiplexer #(.width(7)) multiplexer_1 (
    .in0(keyboard_out), .in1({7{1'b0}}), .out(multiplexer_1_out), .sel(and_1_out));  // open: en
  or or_1 (or_1_out, ~interrupted_this_cycle, and_1_out);  // OR_Gate
  and and_2 (and_2_out, valid_thread_number, interrupted_this_cycle, Op_code_is_RETURN, resolved_interrupt_handler_yet);
  not not_2 (valid_cur_char, comparator_3_eq);
  Comparator #(.width(16)) comparator_4 (.a(Op_code), .b(16'h2400), .eq(comparator_4_eq));  // open: gt, lt
  and and_3 (and_3_out, resolved_interrupt_handler_yet, Op_code_is_RETURN);
  and and_4 (and_4_out, interrupted_this_cycle, Op_code_is_CALL, ~called_interrupted_handler_yet);  // AND_Gate
  and and_5 (and_5_out, interrupted_this_cycle, Op_code_is_RETURN, resolved_interrupt_handler_yet);
  and and_6 (and_6_out, valid_char, ~interrupted_this_cycle);  // AND_Gate
  and and_7 (and_7_out, valid_thread_number, ~interrupted_this_cycle, cycle_number_is_multiple_of_16);  // AND_Gate
  and and_8 (and_8_out, interrupted_this_cycle, Op_code_is_RETURN, resolved_interrupt_handler_yet);
  Register #(.width(7)) register_1 (.D(multiplexer_1_out), .en(or_1_out), .Q(cur_char), .clk(CLK));  // open: clr
  or or_2 (or_2_out, ~valid_thread_number, and_2_out);  // OR_Gate
  and and_9 (valid_cur_char_and_not_return, ~comparator_2_eq, ~Op_code_is_RETURN);  // AND_Gate
  or or_3 (or_3_out, comparator_4_eq, and_3_out);
  Multiplexer multiplexer_2 (.in0(1'b0), .in1(1'b1), .out(multiplexer_2_out), .sel(Op_code_is_CALL));  // open: en
  or or_4 (or_4_out, and_4_out, and_5_out);
  Multiplexer multiplexer_3 (.in0(1'b1), .in1(1'b0), .out(multiplexer_3_out), .sel(and_8_out));  // open: en
  or or_5 (or_5_out, and_6_out, and_7_out, and_8_out);
  and and_10 (and_10_out, or_2_out, ~valid_cur_char);  // AND_Gate
  Register #(.width(1)) register_2 (
    .D(comparator_4_eq), .en(or_3_out), .Q(resolved_interrupt_handler_yet), .clk(CLK));  // open: clr
  Random #(.width(3)) random_1 (.clk(CLK), .next(and_10_out), .out(thread_number));  // open: clr
  Register #(.width(1)) register_3 (
    .D(multiplexer_2_out), .en(or_4_out), .Q(called_interrupted_handler_yet), .clk(CLK));  // open: clr
  Register #(.width(1)) register_4 (
    .D(multiplexer_3_out), .en(or_5_out), .Q(interrupted_this_cycle), .clk(CLK));  // open: clr
  Counter #(.width(4), .max('hf)) counter_1 (.count(1'b1), .Q(counter_1_q), .clk(CLK));  // open: load, D, carry, clr
  BitSelector #(.width(16), .group(8)) bitselector_1 (.in(Op_code), .out(bitselector_1_out), .sel(1'b1));
  BitSelector #(.width(16), .group(8)) bitselector_2 (.in(Op_code), .out(bitselector_2_out), .sel(1'b1));
  Comparator #(.width(3), .mode("unsigned")) comparator_5 (
    .a(thread_number), .b(3'b101), .gt(valid_thread_number));  // open: eq, lt
  Comparator #(.width(4)) comparator_6 (
    .a(counter_1_q), .b(4'b0000), .eq(cycle_number_is_multiple_of_16));  // open: gt, lt
  Comparator comparator_7 (.a(bitselector_1_out), .b(8'h21), .eq(Op_code_is_RETURN));  // open: gt, lt
  Comparator comparator_8 (.a(bitselector_2_out), .b(8'h20), .eq(Op_code_is_CALL));  // open: gt, lt

  // Other names for the same wires on the sheet: called_interrupt_handler_yet = called_interrupted_handler_yet

  // Notes on the sheet:
  //   Cur char is not 0
endmodule
